// Logisim project CPU_change.circ as structural Verilog: 7 circuits, main circuit main
module main (
  input  reset,
  output [31:0] instr,
  output [31:0] pc,
  output RegWrite,
  output [4:0] RegAddr,
  output [31:0] RegData,
  output MemWrite,
  output [31:0] MemAddr,
  output [31:0] MemData
);

  wire clk, Controller_alusrc, Controller_extop, Controller_memtoreg, Controller_npc_sel, Controller_regdst;
  wire [2:0] Controller_aluop;
  wire [31:0] ALU_c, EXT_out_3, GRF_rd1, multiplexer_3_out, ram_1_data;

  Clock clock_1 (.out(clk));
  IFU IFU (
    .clk(clk), .addr(instr[15:0]), .reset(reset), .ifBeq(Controller_npc_sel), .zero(Controller_npc_sel),
    .PC(pc), .instr(instr));
  Controller Controller (
    .ins_31_26(instr[31:26]), .ins_5_0(instr[5:0]), .RegDst(Controller_regdst), .ALUSrc(Controller_alusrc),
    .MemtoReg(Controller_memtoreg), .RegWrite(RegWrite), .MemWrite(MemWrite), .nPC_sel(Controller_npc_sel),
    .ExtOp(Controller_extop), .ALUOp(Controller_aluop));
  Multiplexer #(.width(5), .enable("false")) multiplexer_1 (
    .in0(instr[20:16]), .in1(instr[15:11]), .out(RegAddr), .sel(Controller_regdst));
  Multiplexer #(.width(32), .enable("false")) multiplexer_2 (
    .in0(ALU_c), .in1(ram_1_data), .out(RegData), .sel(Controller_memtoreg));
  EXT EXT (.imm(instr[15:0]), .EXTOp(Controller_extop), .out_3(EXT_out_3));
  GRF GRF (
    .clk(clk), .reset(reset), .WE(RegWrite), .A1(instr[25:21]), .A2(instr[20:16]), .A3(RegAddr),
    .WD(RegData), .RD1(GRF_rd1), .RD2(MemData));
  ALU ALU (.A(GRF_rd1), .B(multiplexer_3_out), .ALUOp(Controller_aluop), .C(ALU_c), .zero(Controller_npc_sel));
  Multiplexer #(.width(32), .enable("false")) multiplexer_3 (
    .in0(MemData), .in1(EXT_out_3), .out(multiplexer_3_out), .sel(Controller_alusrc));
  assign MemAddr = {{20{1'b0}}, ALU_c[11:0]};  // Bit_Extender bit_extender_1
  RAM #(.addrWidth(12), .dataWidth(32), .bus("separate")) ram_1 (
    .addr(ALU_c[11:0]), .din(MemData), .data(ram_1_data), .str(MemWrite), .clk(clk), .clr(reset));  // open: sel, ld
endmodule

module IFU (
  input  clk,
  input  [15:0] addr,
  input  reset,
  input  ifBeq,
  input  zero,
  output [31:0] PC,
  output [31:0] instr
);

  wire and_1_out;
  wire [11:0] bit_extender_2_out, shifter_2_out;
  wire [31:0] adder_1_out, adder_2_out, bit_extender_1_out, multiplexer_1_out, PC_q, shifter_1_out;

  assign bit_extender_1_out = {{16{addr[15]}}, addr};  // Bit_Extender bit_extender_1
  Shifter #(.width(32)) shifter_1 (.in(bit_extender_1_out), .\dist (5'b00010), .out(shifter_1_out));
  Adder #(.width(32)) adder_1 (.a(PC_q), .b(32'h4), .out(adder_1_out));  // open: cin, cout
  Adder #(.width(32)) adder_2 (.a(adder_1_out), .b(shifter_1_out), .out(adder_2_out));  // open: cin, cout
  and and_1 (and_1_out, ifBeq, zero);
  Multiplexer #(.width(32), .enable("false")) multiplexer_1 (
    .in0(adder_1_out), .in1(adder_2_out), .out(multiplexer_1_out), .sel(and_1_out));
  Register #(.width(32)) u_PC (.D(multiplexer_1_out), .Q(PC_q), .clk(clk), .clr(reset));  // open: en
  Adder #(.width(32)) adder_3 (.a(32'h3000), .b(PC_q), .out(PC));  // open: cin, cout
  Bit_Extender #(.in_width(32), .out_width(12)) bit_extender_2 (.in(PC_q), .out(bit_extender_2_out));
  Shifter #(.width(12), .shift("lr")) shifter_2 (.in(bit_extender_2_out), .\dist (4'b0010), .out(shifter_2_out));
  ROM #(.addrWidth(12), .dataWidth(32)) rom_1 (.addr(shifter_2_out), .data(instr));  // open: sel

  // Notes on the sheet:
  //   contents of rom_1 (hex, n*v repeats v):
  //   34090064 340a0060 12a5822 ad690000 8d6c0000 1406820 ad6d0064 11aa0005 0 4*1294820 14a4820 14a4820
  //   14a4820 0 0 0 3c0e1234 35ce5678
endmodule

module ALU (
  input  [31:0] A,
  input  [31:0] B,
  input  [2:0] ALUOp,
  output [31:0] C,
  output zero
);

  wire comparator_1_eq, comparator_2_eq;
  wire [31:0] A_B, A_B_t, A_B_t_t, B_hi;

  Adder #(.width(32)) adder_1 (.a(A), .b(B), .out(A_B));  // open: cin, cout
  Subtractor #(.width(32)) subtractor_1 (.a(A), .b(B), .out(A_B_t));  // open: bin, bout
  Multiplexer #(.select(3), .width(32), .enable("false")) multiplexer_1 (
    .in0(A_B), .in1(A_B_t), .in2(A_B_t_t), .in3(B_hi), .in4({32{1'b0}}), .in5({32{1'b0}}), .in6({32{1'b0}}),
    .in7({32{1'b0}}), .out(C), .sel(ALUOp));
  assign A_B_t_t = A | B;  // OR_Gate or_1, 32 bits wide
  Comparator #(.width(32), .mode("unsigned")) comparator_1 (
    .a(C), .b({32{1'b0}}), .eq(comparator_1_eq));  // open: gt, lt
  Comparator #(.width(3), .mode("unsigned")) comparator_2 (
    .a(ALUOp), .b(3'b001), .eq(comparator_2_eq));  // open: gt, lt
  and and_1 (zero, comparator_1_eq, comparator_2_eq);
  Shifter #(.width(32)) shifter_1 (.in(B), .\dist (5'b10000), .out(B_hi));
endmodule

module Controller (
  input  [5:0] ins_31_26,
  input  [5:0] ins_5_0,
  output RegDst,
  output ALUSrc,
  output MemtoReg,
  output RegWrite,
  output MemWrite,
  output nPC_sel,
  output ExtOp,
  output [2:0] ALUOp
);

  Controller_Change controller_change_1 (
    .RegDst(RegDst), .ALUSrc(ALUSrc), .MemtoReg(MemtoReg), .RegWrite(RegWrite), .MemWrite(MemWrite),
    .nPC_sel(nPC_sel), .ExtOp(ExtOp), .ALUOp_2(ALUOp[2]), .ALUOp_1(ALUOp[1]), .ALUOp_0(ALUOp[0]),
    .ins31(ins_31_26[5]), .ins30(ins_31_26[4]), .ins29(ins_31_26[3]), .ins28(ins_31_26[2]),
    .ins27(ins_31_26[1]), .ins26(ins_31_26[0]), .ins5(ins_5_0[5]), .ins1(ins_5_0[1]));
endmodule

module GRF (
  input  clk,
  input  reset,
  input  WE,
  input  [4:0] A1,
  input  [4:0] A2,
  input  [4:0] A3,
  input  [31:0] WD,
  output [31:0] RD1,
  output [31:0] RD2
);

  wire W1, W2, W3, W4, W5, W6, W7, W8, W9, W10, W11, W12, W13, W14, W15, W16, W17, W18, W19, W20, W21, W22,
       W23, W24, W25, W26, W27, W28, W29, W30, W31;
  wire [4:0] and_1_out, bit_extender_1_out;
  wire [31:0] out2_1, out2_2, out2_3, out2_4, out2_5, out2_6, out2_7, out2_8, out2_9, out2_10, out2_11,
       out2_12, out2_13, out2_14, out2_15, out2_16, out2_17, out2_18, out2_19, out2_20, out2_21, out2_22,
       out2_23, out2_24, out2_25, out2_26, out2_27, out2_28, out2_29, out2_30, out2_31;

  Register #(.width(32)) register_1 (.D(WD), .en(W4), .Q(out2_4), .clk(clk), .clr(reset));
  Register #(.width(32)) register_2 (.D(WD), .en(W8), .Q(out2_8), .clk(clk), .clr(reset));
  Register #(.width(32)) register_3 (.D(WD), .en(W12), .Q(out2_12), .clk(clk), .clr(reset));
  Register #(.width(32)) register_4 (.D(WD), .en(W16), .Q(out2_16), .clk(clk), .clr(reset));
  Register #(.width(32)) register_5 (.D(WD), .en(W20), .Q(out2_20), .clk(clk), .clr(reset));
  Register #(.width(32)) register_6 (.D(WD), .en(W24), .Q(out2_24), .clk(clk), .clr(reset));
  Register #(.width(32)) register_7 (.D(WD), .en(W28), .Q(out2_28), .clk(clk), .clr(reset));
  Multiplexer #(.select(5), .width(32), .enable("false")) multiplexer_1 (
    .in0({32{1'b0}}), .in1(out2_1), .in2(out2_2), .in3(out2_3), .in4(out2_4), .in5(out2_5), .in6(out2_6),
    .in7(out2_7), .in8(out2_8), .in9(out2_9), .in10(out2_10), .in11(out2_11), .in12(out2_12), .in13(out2_13),
    .in14(out2_14), .in15(out2_15), .in16(out2_16), .in17(out2_17), .in18(out2_18), .in19(out2_19),
    .in20(out2_20), .in21(out2_21), .in22(out2_22), .in23(out2_23), .in24(out2_24), .in25(out2_25),
    .in26(out2_26), .in27(out2_27), .in28(out2_28), .in29(out2_29), .in30(out2_30), .in31(out2_31),
    .out(RD1), .sel(A1));
  Register #(.width(32)) register_8 (.D(WD), .en(W1), .Q(out2_1), .clk(clk), .clr(reset));
  Register #(.width(32)) register_9 (.D(WD), .en(W5), .Q(out2_5), .clk(clk), .clr(reset));
  Register #(.width(32)) register_10 (.D(WD), .en(W9), .Q(out2_9), .clk(clk), .clr(reset));
  Register #(.width(32)) register_11 (.D(WD), .en(W13), .Q(out2_13), .clk(clk), .clr(reset));
  Register #(.width(32)) register_12 (.D(WD), .en(W17), .Q(out2_17), .clk(clk), .clr(reset));
  Register #(.width(32)) register_13 (.D(WD), .en(W21), .Q(out2_21), .clk(clk), .clr(reset));
  Register #(.width(32)) register_14 (.D(WD), .en(W25), .Q(out2_25), .clk(clk), .clr(reset));
  Register #(.width(32)) register_15 (.D(WD), .en(W29), .Q(out2_29), .clk(clk), .clr(reset));
  Register #(.width(32)) register_16 (.D(WD), .en(W2), .Q(out2_2), .clk(clk), .clr(reset));
  Register #(.width(32)) register_17 (.D(WD), .en(W6), .Q(out2_6), .clk(clk), .clr(reset));
  Register #(.width(32)) register_18 (.D(WD), .en(W10), .Q(out2_10), .clk(clk), .clr(reset));
  Register #(.width(32)) register_19 (.D(WD), .en(W14), .Q(out2_14), .clk(clk), .clr(reset));
  Register #(.width(32)) register_20 (.D(WD), .en(W18), .Q(out2_18), .clk(clk), .clr(reset));
  Register #(.width(32)) register_21 (.D(WD), .en(W22), .Q(out2_22), .clk(clk), .clr(reset));
  Register #(.width(32)) register_22 (.D(WD), .en(W26), .Q(out2_26), .clk(clk), .clr(reset));
  Register #(.width(32)) register_23 (.D(WD), .en(W30), .Q(out2_30), .clk(clk), .clr(reset));
  Multiplexer #(.select(5), .width(32), .enable("false")) multiplexer_2 (
    .in0({32{1'b0}}), .in1(out2_1), .in2(out2_2), .in3(out2_3), .in4(out2_4), .in5(out2_5), .in6(out2_6),
    .in7(out2_7), .in8(out2_8), .in9(out2_9), .in10(out2_10), .in11(out2_11), .in12(out2_12), .in13(out2_13),
    .in14(out2_14), .in15(out2_15), .in16(out2_16), .in17(out2_17), .in18(out2_18), .in19(out2_19),
    .in20(out2_20), .in21(out2_21), .in22(out2_22), .in23(out2_23), .in24(out2_24), .in25(out2_25),
    .in26(out2_26), .in27(out2_27), .in28(out2_28), .in29(out2_29), .in30(out2_30), .in31(out2_31),
    .out(RD2), .sel(A2));
  Register #(.width(32)) register_24 (.D(WD), .en(W3), .Q(out2_3), .clk(clk), .clr(reset));
  Register #(.width(32)) register_25 (.D(WD), .en(W7), .Q(out2_7), .clk(clk), .clr(reset));
  Register #(.width(32)) register_26 (.D(WD), .en(W11), .Q(out2_11), .clk(clk), .clr(reset));
  Register #(.width(32)) register_27 (.D(WD), .en(W15), .Q(out2_15), .clk(clk), .clr(reset));
  Register #(.width(32)) register_28 (.D(WD), .en(W19), .Q(out2_19), .clk(clk), .clr(reset));
  Register #(.width(32)) register_29 (.D(WD), .en(W23), .Q(out2_23), .clk(clk), .clr(reset));
  Register #(.width(32)) register_30 (.D(WD), .en(W27), .Q(out2_27), .clk(clk), .clr(reset));
  Register #(.width(32)) register_31 (.D(WD), .en(W31), .Q(out2_31), .clk(clk), .clr(reset));
  assign bit_extender_1_out = {{4{WE}}, WE};  // Bit_Extender bit_extender_1
  Decoder #(.select(5), .enable("false")) decoder_1 (
    .out1(W1), .out2(W2), .out3(W3), .out4(W4), .out5(W5), .out6(W6), .out7(W7), .out8(W8), .out9(W9),
    .out10(W10), .out11(W11), .out12(W12), .out13(W13), .out14(W14), .out15(W15), .out16(W16), .out17(W17),
    .out18(W18), .out19(W19), .out20(W20), .out21(W21), .out22(W22), .out23(W23), .out24(W24), .out25(W25),
    .out26(W26), .out27(W27), .out28(W28), .out29(W29), .out30(W30), .out31(W31), .sel(and_1_out));  // open: out0
  assign and_1_out = bit_extender_1_out & A3;  // AND_Gate and_1, 5 bits wide
endmodule

module EXT (
  input  [15:0] imm,
  input  EXTOp,
  output [31:0] out_3
);

  wire [31:0] bit_extender_1_out, bit_extender_2_out;

  assign bit_extender_1_out = {{16{1'b0}}, imm};  // Bit_Extender bit_extender_1
  assign bit_extender_2_out = {{16{imm[15]}}, imm};  // Bit_Extender bit_extender_2
  Multiplexer #(.width(32), .enable("false")) multiplexer_1 (
    .in0(bit_extender_1_out), .in1(bit_extender_2_out), .out(out_3), .sel(EXTOp));
endmodule

module Controller_Change (
  input  ins31,
  input  ins30,
  input  ins29,
  input  ins28,
  input  ins27,
  input  ins26,
  input  ins5,
  input  ins1,
  output RegDst,
  output ALUSrc,
  output MemtoReg,
  output RegWrite,
  output MemWrite,
  output nPC_sel,
  output ExtOp,
  output ALUOp_2,
  output ALUOp_1,
  output ALUOp_0
);

  wire add, beq, lui, lw, nop, not_1_out, not_2_out, not_3_out, not_4_out, not_5_out, not_6_out, not_7_out,
       not_8_out, ori, sub, sw;

  not not_1 (not_1_out, ins31);
  not not_2 (not_2_out, ins30);
  not not_3 (not_3_out, ins28);
  not not_4 (not_4_out, ins29);
  not not_5 (not_5_out, ins5);
  not not_6 (not_6_out, ins26);
  not not_7 (not_7_out, ins27);
  not not_8 (not_8_out, ins1);
  and u_add (add, not_1_out, not_2_out, not_4_out, not_3_out, not_7_out, not_6_out, ins5, not_8_out);
  and u_sub (sub, not_1_out, not_2_out, not_4_out, not_3_out, not_7_out, not_6_out, ins5, ins1);
  and u_ori (ori, not_1_out, not_2_out, ins29, ins28, not_7_out, ins26);
  and u_lw (lw, ins31, not_2_out, not_4_out, not_3_out, ins27, ins26);
  and u_sw (sw, ins31, not_2_out, ins29, not_3_out, ins27, ins26);
  and u_beq (beq, not_1_out, not_2_out, not_4_out, ins28, not_7_out, not_6_out);
  and u_lui (lui, not_1_out, not_2_out, ins29, ins28, ins27, ins26);
  and u_nop (nop, not_1_out, not_2_out, not_4_out, not_3_out, not_7_out, not_6_out, not_5_out, not_8_out);
  or or_1 (RegDst, add, sub);
  or or_2 (ALUSrc, ori, lw, sw, lui);
  or or_3 (MemtoReg, lw, 1'b0);
  or or_4 (RegWrite, add, sub, ori, lw, lui);
  or or_5 (MemWrite, sw, 1'b0);
  or or_6 (nPC_sel, beq, 1'b0);
  or or_7 (ExtOp, lw, sw);
  // OR_Gate or_8 has open pins: in0=1'b0, in1=1'b0, out=open
  or or_9 (ALUOp_1, ori, lui);
  or or_10 (ALUOp_0, sub, beq, lui);

  assign ALUOp_2 = 1'b0;
endmodule
