// Logisim project Logisim_fibonacci_2.circ as structural Verilog: 6 circuits, main circuit main
module main (
  input  [31:0] N,
  output [31:0] out_2
);

  wire clock_1_out, comparator_1_eq, comparator_1_gt, comparator_1_lt, not_1_out, not_2_out, or_1_out;
  wire [4:0] bit_extender_1_out;
  wire [5:0] counter_1_q;
  wire [31:0] adder_1_out, initialize2_1_out_5, initialize2_1_out_6, initialize2_1_out_7,
       initialize2_1_out_8, initialize_1_out_5, initialize_1_out_6, initialize_1_out_7, initialize_1_out_8,
       multiplexer_2_out, multiplexer_3_out, multiplexer_4_out, multiplexer_5_out, multiply_1__1,
       multiply_1__2, multiply_1__3, multiply_1__4, multiply_2__1, multiply_2__2, multiply_2__3,
       multiply_2__4, n_2, register_1_q, register_2_q, register_3_q, register_4_q, register_5_q,
       register_6_q, register_7_q, register_8_q, shifter_1_out;

  // Probe on bit_extender_1_out
  Clock clock_1 (.out(clock_1_out));
  // Probe on multiply_1__4
  // Probe on shifter_1_out
  Shifter #(.width(32), .shift("lr")) shifter_1 (.in(n_2), .\dist (bit_extender_1_out), .out(shifter_1_out));
  Counter #(.width(6), .max('h3f), .ongoal("stay")) counter_1 (
    .Q(counter_1_q), .clk(clock_1_out));  // open: load, D, count, carry, clr
  Bit_Extender #(.in_width(6), .out_width(5)) bit_extender_1 (.in(counter_1_q), .out(bit_extender_1_out));
  // Probe on shifter_1_out[0]
  Comparator #(.width(6), .mode("unsigned")) comparator_1 (
    .a(counter_1_q), .b(6'b100000), .gt(comparator_1_gt), .eq(comparator_1_eq), .lt(comparator_1_lt));
  Adder #(.width(32)) adder_1 (.a(register_5_q), .b(register_6_q), .out(adder_1_out));  // open: cin, cout
  Subtractor #(.width(32)) subtractor_1 (.a(N), .b(32'h2), .out(n_2));  // open: bin, bout
  initialize initialize_1 (
    .in_1(register_1_q), .in_2(register_3_q), .in_3(register_2_q), .in_4(register_4_q),
    .out_5(initialize_1_out_5), .out_6(initialize_1_out_6), .out_7(initialize_1_out_7),
    .out_8(initialize_1_out_8));
  or or_1 (or_1_out, comparator_1_gt, comparator_1_eq);
  not not_1 (not_1_out, comparator_1_lt);
  multiply multiply_1 (
    ._100(initialize_1_out_5), ._101(initialize_1_out_6), ._110(initialize_1_out_7),
    ._111(initialize_1_out_8), ._200(initialize_1_out_5), ._201(initialize_1_out_6),
    ._210(initialize_1_out_7), ._211(initialize_1_out_8), ._1(multiply_1__1), ._2(multiply_1__2),
    ._3(multiply_1__3), ._4(multiply_1__4));
  not not_2 (not_2_out, or_1_out);
  Register #(.width(32)) register_1 (.D(multiply_1__1), .Q(register_1_q), .clk(clock_1_out));  // open: en, clr
  Register #(.width(32)) register_2 (.D(multiply_1__3), .Q(register_2_q), .clk(clock_1_out));  // open: en, clr
  Multiplexer #(.width(32)) multiplexer_1 (
    .in0({32{1'b0}}), .in1(adder_1_out), .out(out_2), .sel(not_1_out));  // open: en
  Register #(.width(32)) register_3 (.D(multiply_1__2), .Q(register_3_q), .clk(clock_1_out));  // open: en, clr
  Register #(.width(32)) register_4 (.D(multiply_1__4), .Q(register_4_q), .clk(clock_1_out));  // open: en, clr
  initialize2 initialize2_1 (
    .in_1(register_5_q), .in_2(register_6_q), .in_3(register_7_q), .in_4(register_8_q),
    .out_5(initialize2_1_out_5), .out_6(initialize2_1_out_6), .out_7(initialize2_1_out_7),
    .out_8(initialize2_1_out_8));
  multiply multiply_2 (
    ._100(initialize2_1_out_5), ._101(initialize2_1_out_6), ._110(initialize2_1_out_7),
    ._111(initialize2_1_out_8), ._200(initialize_1_out_5), ._201(initialize_1_out_6),
    ._210(initialize_1_out_7), ._211(initialize_1_out_8), ._1(multiply_2__1), ._2(multiply_2__2),
    ._3(multiply_2__3), ._4(multiply_2__4));
  Multiplexer #(.width(32)) multiplexer_2 (
    .in0(initialize2_1_out_5), .in1(multiply_2__1), .out(multiplexer_2_out), .sel(shifter_1_out[0]));  // open: en
  Multiplexer #(.width(32)) multiplexer_3 (
    .in0(initialize2_1_out_6), .in1(multiply_2__2), .out(multiplexer_3_out), .sel(shifter_1_out[0]));  // open: en
  Multiplexer #(.width(32)) multiplexer_4 (
    .in0(initialize2_1_out_7), .in1(multiply_2__3), .out(multiplexer_4_out), .sel(shifter_1_out[0]));  // open: en
  Multiplexer #(.width(32)) multiplexer_5 (
    .in0(initialize2_1_out_8), .in1(multiply_2__4), .out(multiplexer_5_out), .sel(shifter_1_out[0]));  // open: en
  Register #(.width(32)) register_5 (
    .D(multiplexer_2_out), .en(not_2_out), .Q(register_5_q), .clk(clock_1_out));  // open: clr
  Register #(.width(32)) register_6 (
    .D(multiplexer_3_out), .en(not_2_out), .Q(register_6_q), .clk(clock_1_out));  // open: clr
  Register #(.width(32)) register_7 (
    .D(multiplexer_4_out), .en(not_2_out), .Q(register_7_q), .clk(clock_1_out));  // open: clr
  Register #(.width(32)) register_8 (
    .D(multiplexer_5_out), .en(not_2_out), .Q(register_8_q), .clk(clock_1_out));  // open: clr
endmodule

module multiply (
  input  [31:0] _100,
  input  [31:0] _101,
  input  [31:0] _110,
  input  [31:0] _111,
  input  [31:0] _200,
  input  [31:0] _201,
  input  [31:0] _210,
  input  [31:0] _211,
  output [31:0] _1,
  output [31:0] _2,
  output [31:0] _3,
  output [31:0] _4
);

  wire [31:0] multiplier_1_out, multiplier_2_out, multiplier_3_out, multiplier_4_out, multiplier_5_out,
       multiplier_6_out, multiplier_7_out, multiplier_8_out;

  Multiplier #(.width(32)) multiplier_1 (.a(_100), .b(_200), .out(multiplier_1_out));  // open: cin, cout
  Multiplier #(.width(32)) multiplier_2 (.a(_101), .b(_210), .out(multiplier_2_out));  // open: cin, cout
  Adder #(.width(32)) adder_1 (.a(multiplier_1_out), .b(multiplier_2_out), .out(_1));  // open: cin, cout
  Multiplier #(.width(32)) multiplier_3 (.a(_100), .b(_201), .out(multiplier_3_out));  // open: cin, cout
  Multiplier #(.width(32)) multiplier_4 (.a(_101), .b(_211), .out(multiplier_4_out));  // open: cin, cout
  Adder #(.width(32)) adder_2 (.a(multiplier_3_out), .b(multiplier_4_out), .out(_2));  // open: cin, cout
  Multiplier #(.width(32)) multiplier_5 (.a(_110), .b(_200), .out(multiplier_5_out));  // open: cin, cout
  Multiplier #(.width(32)) multiplier_6 (.a(_111), .b(_210), .out(multiplier_6_out));  // open: cin, cout
  Adder #(.width(32)) adder_3 (.a(multiplier_5_out), .b(multiplier_6_out), .out(_3));  // open: cin, cout
  Multiplier #(.width(32)) multiplier_7 (.a(_110), .b(_201), .out(multiplier_7_out));  // open: cin, cout
  Multiplier #(.width(32)) multiplier_8 (.a(_111), .b(_211), .out(multiplier_8_out));  // open: cin, cout
  Adder #(.width(32)) adder_4 (.a(multiplier_7_out), .b(multiplier_8_out), .out(_4));  // open: cin, cout
endmodule

module E (
  output [31:0] out_1,
  output [31:0] out_2,
  output [31:0] out_3,
  output [31:0] out_4
);


  assign out_1 = 32'h1;
  assign out_2 = {32{1'b0}};
  assign out_3 = {32{1'b0}};
  assign out_4 = 32'h1;
endmodule

module C (
  output [31:0] out_1,
  output [31:0] out_2,
  output [31:0] out_3,
  output [31:0] out_4
);


  assign out_1 = 32'h1;
  assign out_2 = 32'h1;
  assign out_3 = 32'h1;
  assign out_4 = {32{1'b0}};
endmodule

module initialize (
  input  [31:0] in_1,
  input  [31:0] in_2,
  input  [31:0] in_3,
  input  [31:0] in_4,
  output [31:0] out_5,
  output [31:0] out_6,
  output [31:0] out_7,
  output [31:0] out_8
);

  wire comparator_1_eq;
  wire [31:0] adder_1_out, adder_2_out, adder_3_out;

  Adder #(.width(32)) adder_1 (.a(in_1), .b(in_2), .out(adder_1_out));  // open: cin, cout
  Adder #(.width(32)) adder_2 (.a(in_3), .b(in_4), .out(adder_2_out));  // open: cin, cout
  Adder #(.width(32)) adder_3 (.a(adder_1_out), .b(adder_2_out), .out(adder_3_out));  // open: cin, cout
  Multiplexer #(.width(32)) multiplexer_1 (.in0(in_1), .in1(32'h1), .out(out_5), .sel(comparator_1_eq));  // open: en
  Comparator #(.width(32), .mode("unsigned")) comparator_1 (
    .a(adder_3_out), .b({32{1'b0}}), .eq(comparator_1_eq));  // open: gt, lt
  Multiplexer #(.width(32)) multiplexer_2 (.in0(in_2), .in1(32'h1), .out(out_6), .sel(comparator_1_eq));  // open: en
  Multiplexer #(.width(32)) multiplexer_3 (.in0(in_3), .in1(32'h1), .out(out_7), .sel(comparator_1_eq));  // open: en
  Multiplexer #(.width(32)) multiplexer_4 (
    .in0(in_4), .in1({32{1'b0}}), .out(out_8), .sel(comparator_1_eq));  // open: en
endmodule

module initialize2 (
  input  [31:0] in_1,
  input  [31:0] in_2,
  input  [31:0] in_3,
  input  [31:0] in_4,
  output [31:0] out_5,
  output [31:0] out_6,
  output [31:0] out_7,
  output [31:0] out_8
);

  wire comparator_1_eq;
  wire [31:0] adder_1_out, adder_2_out, adder_3_out;

  Adder #(.width(32)) adder_1 (.a(in_1), .b(in_2), .out(adder_1_out));  // open: cin, cout
  Adder #(.width(32)) adder_2 (.a(in_3), .b(in_4), .out(adder_2_out));  // open: cin, cout
  Adder #(.width(32)) adder_3 (.a(adder_1_out), .b(adder_2_out), .out(adder_3_out));  // open: cin, cout
  Multiplexer #(.width(32)) multiplexer_1 (.in0(in_1), .in1(32'h1), .out(out_5), .sel(comparator_1_eq));  // open: en
  Comparator #(.width(32), .mode("unsigned")) comparator_1 (
    .a(adder_3_out), .b({32{1'b0}}), .eq(comparator_1_eq));  // open: gt, lt
  Multiplexer #(.width(32)) multiplexer_2 (
    .in0(in_2), .in1({32{1'b0}}), .out(out_6), .sel(comparator_1_eq));  // open: en
  Multiplexer #(.width(32)) multiplexer_3 (
    .in0(in_3), .in1({32{1'b0}}), .out(out_7), .sel(comparator_1_eq));  // open: en
  Multiplexer #(.width(32)) multiplexer_4 (.in0(in_4), .in1(32'h1), .out(out_8), .sel(comparator_1_eq));  // open: en
endmodule
