// Logisim project P0_L0_CRC.circ as structural Verilog: 3 circuits, main circuit CRC
module CRC (
  input  [7:0] A,
  input  [3:0] B,
  output [10:0] C
);

  wire [0:0] shift_12_out_4;
  wire [3:0] shift_1_out_4, shift_2_out_4, shift_3_out_4, shift_4_out_4, shift_5_out_4, shift_6_out_4,
       shift_7_out_4, shift_8_out_4, shift_9_out_4, shift_10_out_4, shift_11_out_4;
  wire [10:0] in_1_out_2;

  in in_1 (.in_1(A), .out_2(in_1_out_2));
  shift shift_1 (.in_1(in_1_out_2[10]), .in_2(B), .in_3(4'b0000), .out_4(shift_1_out_4));
  shift shift_2 (.in_1(in_1_out_2[9]), .in_2(B), .in_3(shift_1_out_4), .out_4(shift_2_out_4));
  shift shift_3 (.in_1(in_1_out_2[8]), .in_2(B), .in_3(shift_2_out_4), .out_4(shift_3_out_4));
  shift shift_4 (.in_1(in_1_out_2[6]), .in_2(B), .in_3(shift_5_out_4), .out_4(shift_4_out_4));
  shift shift_5 (.in_1(in_1_out_2[7]), .in_2(B), .in_3(shift_3_out_4), .out_4(shift_5_out_4));
  shift shift_6 (.in_1(in_1_out_2[5]), .in_2(B), .in_3(shift_4_out_4), .out_4(shift_6_out_4));
  shift shift_7 (.in_1(in_1_out_2[3]), .in_2(B), .in_3(shift_8_out_4), .out_4(shift_7_out_4));
  shift shift_8 (.in_1(in_1_out_2[4]), .in_2(B), .in_3(shift_6_out_4), .out_4(shift_8_out_4));
  shift shift_9 (.in_1(in_1_out_2[2]), .in_2(B), .in_3(shift_7_out_4), .out_4(shift_9_out_4));
  shift shift_10 (.in_1(in_1_out_2[1]), .in_2(B), .in_3(shift_9_out_4), .out_4(shift_10_out_4));
  shift shift_11 (.in_1(in_1_out_2[0]), .in_2(B), .in_3(shift_10_out_4), .out_4(shift_11_out_4));
  shift shift_12 (.in_1(1'b0), .in_2(B), .in_3(shift_11_out_4), .out_4({C[2:0], shift_12_out_4[0]}));

  assign C[10:3] = A;

  // Other names for the same wires on the sheet: in[7:0] = A
endmodule

module shift (
  input  in_1,
  input  [3:0] in_2,
  input  [3:0] in_3,
  output [3:0] out_4
);

  wire [3:0] xor_1_out;

  assign xor_1_out = in_2 ^ in_3;  // XOR_Gate xor_1, 4 bits wide
  Multiplexer #(.width(4)) multiplexer_1 (
    .in0({in_3[2:0], in_1}), .in1({xor_1_out[2:0], in_1}), .out(out_4), .sel(in_3[3]));  // open: en
endmodule

module in (
  input  [7:0] in_1,
  output [10:0] out_2
);

  wire [10:0] bit_extender_1_out;

  assign bit_extender_1_out = {{3{1'b0}}, in_1};  // Bit_Extender bit_extender_1
  // Probe on out_2
  Shifter #(.width(11)) shifter_1 (.in(bit_extender_1_out), .\dist (4'b0011), .out(out_2));
endmodule
