// Logisim project P0_L0_FSM.circ as structural Verilog: 3 circuits, main circuit fsm
module fsm (
  input  [1:0] In,
  input  CLR,
  output Z
);

  wire clock_1_out;
  wire [1:0] multiplexer_1_out, status, sub_1_next_status;

  // Probe on status
  sub sub_1 (.In(In), .status(status), .next_status(sub_1_next_status));
  Register #(.width(2)) register_1 (.D(multiplexer_1_out), .Q(status), .clk(clock_1_out));  // open: en, clr
  Multiplexer #(.width(2)) multiplexer_1 (
    .in0(sub_1_next_status), .in1(2'b00), .out(multiplexer_1_out), .sel(CLR));  // open: en
  Clock clock_1 (.out(clock_1_out));
  print print_1 (.in_1(In), .in_2(status), .o0(Z));
endmodule

module sub (
  input  [1:0] In,
  input  [1:0] status,
  output [1:0] next_status
);

  wire and_1_out, and_2_out, and_3_out, and_4_out, and_5_out, and_6_out, and_7_out, and_8_out, not_1_out,
       not_2_out, not_3_out, not_4_out, not_5_out, not_6_out, not_7_out, not_8_out, not_9_out, not_10_out,
       not_11_out, not_12_out, not_13_out, not_14_out, not_15_out, not_16_out;

  not not_1 (not_1_out, In[1]);
  and and_1 (and_1_out, not_1_out, not_2_out, status[0]);
  not not_2 (not_2_out, status[1]);
  not not_3 (not_3_out, In[0]);
  not not_4 (not_4_out, status[1]);
  and and_2 (and_2_out, not_3_out, not_4_out, status[0]);
  not not_5 (not_5_out, In[1]);
  and and_3 (and_3_out, not_5_out, status[1], not_6_out);
  not not_6 (not_6_out, status[0]);
  not not_7 (not_7_out, In[0]);
  and and_4 (and_4_out, not_7_out, status[1], not_8_out);
  not not_8 (not_8_out, status[0]);
  not not_9 (not_9_out, In[0]);
  not not_10 (not_10_out, status[1]);
  not not_11 (not_11_out, In[0]);
  not not_12 (not_12_out, status[0]);
  not not_13 (not_13_out, In[1]);
  not not_14 (not_14_out, status[1]);
  not not_15 (not_15_out, status[0]);
  not not_16 (not_16_out, In[1]);
  or or_1 (next_status[1], and_1_out, and_2_out, and_3_out, and_4_out);
  and and_5 (and_5_out, not_9_out, not_10_out, status[0]);
  and and_6 (and_6_out, not_11_out, status[1], not_12_out);
  and and_7 (and_7_out, not_13_out, In[0], not_14_out, not_15_out);
  and and_8 (and_8_out, not_16_out, In[0], status[1], status[0]);
  or or_2 (next_status[0], and_5_out, and_6_out, and_7_out, and_8_out);
endmodule

module print (
  input  [1:0] in_1,
  input  [1:0] in_2,
  output o0
);

  wire not_1_out;

  not not_1 (not_1_out, in_1[0]);
  and and_1 (o0, not_1_out, in_2[1], in_2[0]);
endmodule
