// Logisim project P0_L0_GRF.circ as structural Verilog: 5 circuits, main circuit grf
module grf (
  input  [4:0] A1,
  input  [4:0] A2,
  input  reset,
  input  clk,
  input  [31:0] WD,
  input  [4:0] A3,
  input  WE,
  output [31:0] RD1,
  output [31:0] RD2
);

  wire [4:0] and_1_out, bit_extender_1_out;
  wire [31:0] _0, _1, _2, _3, _4, _5, _6, _7, _8, _9, _10, _11, _12, _13, _14, _15, _16, _17, _18, _19, _20,
       _21, _22, _23, _24, _25, _26, _27, _28, _29, _30, _31, WD0, WD1, WD2, WD3, WD4, WD5, WD6, WD7, WD8,
       WD9, WD10, WD11, WD12, WD13, WD14, WD15, WD16, WD17, WD18, WD19, WD20, WD21, WD22, WD23, WD24, WD25,
       WD26, WD27, WD28, WD29, WD30, WD31;

  assign bit_extender_1_out = {{4{WE}}, WE};  // Bit_Extender bit_extender_1
  Register #(.width(32)) register_1 (.D(WD0), .Q(_0), .clk(clk), .clr(reset));  // open: en
  Register #(.width(32)) register_2 (.D(WD8), .Q(_8), .clk(clk), .clr(reset));  // open: en
  Register #(.width(32)) register_3 (.D(WD16), .Q(_16), .clk(clk), .clr(reset));  // open: en
  Register #(.width(32)) register_4 (.D(WD24), .Q(_24), .clk(clk), .clr(reset));  // open: en
  // Probe on and_1_out
  assign and_1_out = A3 & bit_extender_1_out;  // AND_Gate and_1, 5 bits wide
  // Probe on WD1
  Demultiplexer #(.select(5), .width(32), .tristate("true")) demultiplexer_1 (
    .out1(WD1), .out2(WD2), .out3(WD3), .out4(WD4), .out5(WD5), .out6(WD6), .out7(WD7), .out8(WD8),
    .out9(WD9), .out10(WD10), .out11(WD11), .out12(WD12), .out13(WD13), .out14(WD14), .out15(WD15),
    .out16(WD16), .out17(WD17), .out18(WD18), .out19(WD19), .out20(WD20), .out21(WD21), .out22(WD22),
    .out23(WD23), .out24(WD24), .out25(WD25), .out26(WD26), .out27(WD27), .out28(WD28), .out29(WD29),
    .out30(WD30), .out31(WD31), .in(WD), .sel(and_1_out));  // open: out0, en
  Register #(.width(32)) register_5 (.D(WD1), .Q(_1), .clk(clk), .clr(reset));  // open: en
  Register #(.width(32)) register_6 (.D(WD9), .Q(_9), .clk(clk), .clr(reset));  // open: en
  Register #(.width(32)) register_7 (.D(WD17), .Q(_17), .clk(clk), .clr(reset));  // open: en
  Register #(.width(32)) register_8 (.D(WD25), .Q(_25), .clk(clk), .clr(reset));  // open: en
  Register #(.width(32)) register_9 (.D(WD2), .Q(_2), .clk(clk), .clr(reset));  // open: en
  Register #(.width(32)) register_10 (.D(WD10), .Q(_10), .clk(clk), .clr(reset));  // open: en
  Register #(.width(32)) register_11 (.D(WD18), .Q(_18), .clk(clk), .clr(reset));  // open: en
  Register #(.width(32)) register_12 (.D(WD26), .Q(_26), .clk(clk), .clr(reset));  // open: en
  Register #(.width(32)) register_13 (.D(WD3), .Q(_3), .clk(clk), .clr(reset));  // open: en
  Register #(.width(32)) register_14 (.D(WD11), .Q(_11), .clk(clk), .clr(reset));  // open: en
  Register #(.width(32)) register_15 (.D(WD19), .Q(_19), .clk(clk), .clr(reset));  // open: en
  Register #(.width(32)) register_16 (.D(WD27), .Q(_27), .clk(clk), .clr(reset));  // open: en
  Register #(.width(32)) register_17 (.D(WD4), .Q(_4), .clk(clk), .clr(reset));  // open: en
  Register #(.width(32)) register_18 (.D(WD12), .Q(_12), .clk(clk), .clr(reset));  // open: en
  Register #(.width(32)) register_19 (.D(WD20), .Q(_20), .clk(clk), .clr(reset));  // open: en
  Register #(.width(32)) register_20 (.D(WD28), .Q(_28), .clk(clk), .clr(reset));  // open: en
  // Probe on _0
  Register #(.width(32)) register_21 (.D(WD5), .Q(_5), .clk(clk), .clr(reset));  // open: en
  Register #(.width(32)) register_22 (.D(WD13), .Q(_13), .clk(clk), .clr(reset));  // open: en
  Register #(.width(32)) register_23 (.D(WD21), .Q(_21), .clk(clk), .clr(reset));  // open: en
  Register #(.width(32)) register_24 (.D(WD29), .Q(_29), .clk(clk), .clr(reset));  // open: en
  Register #(.width(32)) register_25 (.D(WD6), .Q(_6), .clk(clk), .clr(reset));  // open: en
  Register #(.width(32)) register_26 (.D(WD14), .Q(_14), .clk(clk), .clr(reset));  // open: en
  Register #(.width(32)) register_27 (.D(WD22), .Q(_22), .clk(clk), .clr(reset));  // open: en
  Register #(.width(32)) register_28 (.D(WD30), .Q(_30), .clk(clk), .clr(reset));  // open: en
  Multiplexer #(.select(5), .width(32)) multiplexer_1 (
    .in0(_0), .in1(_1), .in2(_2), .in3(_3), .in4(_4), .in5(_5), .in6(_6), .in7(_7), .in8(_8), .in9(_9),
    .in10(_10), .in11(_11), .in12(_12), .in13(_13), .in14(_14), .in15(_15), .in16(_16), .in17(_17),
    .in18(_18), .in19(_19), .in20(_20), .in21(_21), .in22(_22), .in23(_23), .in24(_24), .in25(_25),
    .in26(_26), .in27(_27), .in28(_28), .in29(_29), .in30(_30), .in31(_31), .out(RD2), .sel(A2));  // open: en
  Register #(.width(32)) register_29 (.D(WD7), .Q(_7), .clk(clk), .clr(reset));  // open: en
  Register #(.width(32)) register_30 (.D(WD15), .Q(_15), .clk(clk), .clr(reset));  // open: en
  Register #(.width(32)) register_31 (.D(WD23), .Q(_23), .clk(clk), .clr(reset));  // open: en
  Register #(.width(32)) register_32 (.D(WD31), .Q(_31), .clk(clk), .clr(reset));  // open: en
  // Probe on _0
  Multiplexer #(.select(5), .width(32)) multiplexer_2 (
    .in0(_0), .in1(_1), .in2(_2), .in3(_3), .in4(_4), .in5(_5), .in6(_6), .in7(_7), .in8(_8), .in9(_9),
    .in10(_10), .in11(_11), .in12(_12), .in13(_13), .in14(_14), .in15(_15), .in16(_16), .in17(_17),
    .in18(_18), .in19(_19), .in20(_20), .in21(_21), .in22(_22), .in23(_23), .in24(_24), .in25(_25),
    .in26(_26), .in27(_27), .in28(_28), .in29(_29), .in30(_30), .in31(_31), .out(RD1), .sel(A1));  // open: en

  // Other names for the same wires on the sheet: d1[31:0] = RD1; d2[31:0] = RD2
endmodule

module enable (
  input  [31:0] in_1,
  input  [4:0] in_2,
  input  in_3
);

  wire [4:0] and_1_out, bit_extender_1_out;
  wire [31:0] WD1, WD2, WD3, WD4, WD5, WD6, WD7, WD8, WD9, WD10, WD11, WD12, WD13, WD14, WD15, WD16, WD17,
       WD18, WD19, WD20, WD21, WD22, WD23, WD24, WD25, WD26, WD27, WD28, WD29, WD30, WD31;

  assign bit_extender_1_out = {{4{in_3}}, in_3};  // Bit_Extender bit_extender_1
  assign and_1_out = in_2 & bit_extender_1_out;  // AND_Gate and_1, 5 bits wide
  // Probe on and_1_out
  Demultiplexer #(.select(5), .width(32)) demultiplexer_1 (
    .out1(WD1), .out2(WD2), .out3(WD3), .out4(WD4), .out5(WD5), .out6(WD6), .out7(WD7), .out8(WD8),
    .out9(WD9), .out10(WD10), .out11(WD11), .out12(WD12), .out13(WD13), .out14(WD14), .out15(WD15),
    .out16(WD16), .out17(WD17), .out18(WD18), .out19(WD19), .out20(WD20), .out21(WD21), .out22(WD22),
    .out23(WD23), .out24(WD24), .out25(WD25), .out26(WD26), .out27(WD27), .out28(WD28), .out29(WD29),
    .out30(WD30), .out31(WD31), .in(in_1), .sel(and_1_out));  // open: out0, en
endmodule

module out1 (
  input  [4:0] in_1,
  output [31:0] out_2
);

  wire [31:0] _0, _1, _2, _3, _4, _5, _6, _7, _8, _9, _10, _11, _12, _13, _14, _15, _16, _17, _18, _19, _20,
       _21, _22, _23, _24, _25, _26, _27, _28, _29, _30, _31;

  Multiplexer #(.select(5), .width(32)) multiplexer_1 (
    .in0(_0), .in1(_1), .in2(_2), .in3(_3), .in4(_4), .in5(_5), .in6(_6), .in7(_7), .in8(_8), .in9(_9),
    .in10(_10), .in11(_11), .in12(_12), .in13(_13), .in14(_14), .in15(_15), .in16(_16), .in17(_17),
    .in18(_18), .in19(_19), .in20(_20), .in21(_21), .in22(_22), .in23(_23), .in24(_24), .in25(_25),
    .in26(_26), .in27(_27), .in28(_28), .in29(_29), .in30(_30), .in31(_31), .out(out_2), .sel(in_1));  // open: en
endmodule

module main (
  input  reset,
  output [31:0] Instr,
  output [31:0] pc,
  output RegWrite,
  output [4:0] RegAddr,
  output [31:0] RegData,
  output MemWrite,
  output [31:0] MenAddr,
  output [31:0] MenData
);

  wire clk, PCop;
  wire [5:0] Func;
  wire [15:0] beq, PC_t, PCshift_out_4;
  wire [25:0] insprobe;

  Clock clock_1 (.out(clk));
  PCshift PCshift (.in_1(PCop), .in_2(beq), .in_3(PC_t), .out_4(PCshift_out_4));
  Register #(.width(16)) register_1 (.D(PCshift_out_4), .Q(PC_t), .clk(clk), .clr(reset));  // open: en
  // Probe on {Func, insprobe}
  // Probe on insprobe[5:0]
  // Probe on Func
  ROM #(.addrWidth(16), .dataWidth(32)) rom_1 (.addr(PC_t), .data({Func, insprobe}));  // open: sel
  grf GRF ();  // open: clk, reset, WE, A1, A2, A3, WD, RD1, RD2
  RAM #(.bus("separate")) ram_1 ();  // open: addr, din, data, str, sel, clk, ld, clr

  // Other names for the same wires on the sheet: funcprobe[5:0] = Func; insprobe[31:26] = Func;
  //   instruction[31:0] = {Func, insprobe}; Op[5:0] = insprobe[5:0]; Oppreobe[5:0] = insprobe[5:0]
endmodule

module PCshift (
  input  in_1,
  input  [15:0] in_2,
  input  [15:0] in_3,
  output [15:0] out_4
);

  wire [15:0] adder_1_out, adder_2_out;

  Adder #(.width(16)) adder_1 (.a(in_3), .b(16'h4), .out(adder_1_out));  // open: cin, cout
  Adder #(.width(16)) adder_2 (.a(in_2), .b(adder_1_out), .out(adder_2_out));  // open: cin, cout
  Multiplexer #(.width(16)) multiplexer_1 (.in0(adder_1_out), .in1(adder_2_out), .out(out_4), .sel(in_1));  // open: en

  // Other names for the same wires on the sheet: PCop = in_1
endmodule
