// Logisim project P0_L1_ftoi.circ as structural Verilog: 4 circuits, main circuit ftoi
module ftoi (
  input  [15:0] float,
  output [31:0] \int 
);

  wire [1:0] \type ;
  wire [4:0] adder_1_out;
  wire [31:0] c2_1_out_3, calculate_1_out_3, multiplexer_1_out, negator_1_out;

  // Probe on float[9:0]
  // Probe on \type 
  \type  type_1 (.in_1(float[14:10]), .out_2(\type ));
  Adder #(.width(5)) adder_1 (.a(float[14:10]), .b(5'b10001), .out(adder_1_out));  // open: cin, cout
  // Probe on adder_1_out
  calculate calculate_1 (.in_1(float[9:0]), .in_2(adder_1_out), .out_3(calculate_1_out_3));
  c2 c2_1 (.in_1(float[9:0]), .in_2(adder_1_out), .out_3(c2_1_out_3));
  // Probe on multiplexer_1_out
  Multiplexer #(.select(2), .width(32)) multiplexer_1 (
    .in0(calculate_1_out_3), .in1({32{1'b0}}), .in2({32{1'b0}}), .in3({32{1'b0}}), .out(multiplexer_1_out),
    .sel(\type ));  // open: en
  Negator #(.width(32)) negator_1 (.in(multiplexer_1_out), .out(negator_1_out));
  Multiplexer #(.width(32)) multiplexer_2 (
    .in0(multiplexer_1_out), .in1(negator_1_out), .out(\int ), .sel(float[15]));  // open: en

  // Other names for the same wires on the sheet: fraction[9:0] = float[9:0]; exponet[4:0] = float[14:10];
  //   sign = float[15]
endmodule

module \type  (
  input  [4:0] in_1,
  output [1:0] out_2
);

  wire comparator_1_eq;

  Comparator #(.width(5)) comparator_1 (.a(in_1), .b({5{1'b0}}), .eq(comparator_1_eq));  // open: gt, lt
  Comparator #(.width(5)) comparator_2 (.a(in_1), .b({5{1'b1}}), .eq(out_2[1]));  // open: gt, lt
  or or_1 (out_2[0], comparator_1_eq, out_2[1]);
endmodule

module calculate (
  input  [9:0] in_1,
  input  [4:0] in_2,
  output [31:0] out_3
);

  wire comparator_1_lt, comparator_2_eq, undriven, undriven_2;
  wire [4:0] negator_1_out, subtractor_1_out;
  wire [10:0] bit_extender_1_out;
  wire [31:0] bit_extender_2_out, multiplexer_1_out, multiplexer_2_out, shifter_1_out, shifter_2_out;

  Subtractor #(.width(5)) subtractor_1 (.a(5'b01010), .b(in_2), .out(subtractor_1_out));  // open: bin, bout
  // Probe on subtractor_1_out
  // Probe on undriven
  assign bit_extender_1_out = {{1{1'b1}}, in_1};  // Bit_Extender bit_extender_1
  assign bit_extender_2_out = {{21{1'b0}}, bit_extender_1_out};  // Bit_Extender bit_extender_2
  // Probe on undriven_2
  Comparator #(.width(5)) comparator_1 (.a(subtractor_1_out), .b({5{1'b0}}), .lt(comparator_1_lt));  // open: gt, eq
  Negator #(.width(5)) negator_1 (.in(subtractor_1_out), .out(negator_1_out));
  // Probe on bit_extender_2_out
  Shifter #(.width(32), .shift("lr")) shifter_1 (
    .in(bit_extender_2_out), .\dist (subtractor_1_out), .out(shifter_1_out));
  Comparator #(.width(5)) comparator_2 (.a(in_2), .b({5{1'b0}}), .eq(comparator_2_eq));  // open: gt, lt
  Multiplexer #(.width(32)) multiplexer_1 (
    .in0(shifter_1_out), .in1(shifter_2_out), .out(multiplexer_1_out), .sel(comparator_1_lt));  // open: en
  Multiplexer #(.width(32)) multiplexer_2 (
    .in0(multiplexer_1_out), .in1({32{1'b0}}), .out(multiplexer_2_out), .sel(in_2[4]));  // open: en
  Shifter #(.width(32)) shifter_2 (.in(bit_extender_2_out), .\dist (negator_1_out), .out(shifter_2_out));
  Multiplexer #(.width(32)) multiplexer_3 (
    .in0(multiplexer_2_out), .in1(32'h1), .out(out_3), .sel(comparator_2_eq));  // open: en
endmodule

module c2 (
  input  [9:0] in_1,
  input  [4:0] in_2,
  output [31:0] out_3
);

  wire comparator_1_eq, undriven, undriven_2;
  wire [3:0] negator_1_out, subtractor_1_out;
  wire [4:0] bit_extender_3_out, bit_extender_4_out;
  wire [10:0] bit_extender_1_out;
  wire [31:0] bit_extender_2_out, multiplexer_1_out, multiplexer_2_out, shifter_1_out, shifter_2_out;

  Subtractor #(.width(4)) subtractor_1 (.a(4'b1010), .b(in_2[3:0]), .out(subtractor_1_out));  // open: bin, bout
  // Probe on subtractor_1_out
  // Probe on undriven
  assign bit_extender_1_out = {{1{1'b0}}, in_1};  // Bit_Extender bit_extender_1
  assign bit_extender_2_out = {{21{1'b0}}, bit_extender_1_out};  // Bit_Extender bit_extender_2
  // Probe on undriven_2
  Shifter #(.width(32), .shift("lr")) shifter_1 (
    .in(bit_extender_2_out), .\dist (bit_extender_3_out), .out(shifter_1_out));
  assign bit_extender_3_out = {{1{1'b0}}, subtractor_1_out};  // Bit_Extender bit_extender_3
  // Probe on bit_extender_2_out
  Multiplexer #(.width(32)) multiplexer_1 (
    .in0(shifter_1_out), .in1(shifter_2_out), .out(multiplexer_1_out), .sel(subtractor_1_out[3]));  // open: en
  Comparator #(.width(5)) comparator_1 (.a(in_2), .b({5{1'b0}}), .eq(comparator_1_eq));  // open: gt, lt
  Shifter #(.width(32)) shifter_2 (.in(bit_extender_2_out), .\dist (bit_extender_4_out), .out(shifter_2_out));
  Multiplexer #(.width(32)) multiplexer_2 (
    .in0(multiplexer_1_out), .in1({32{1'b0}}), .out(multiplexer_2_out), .sel(in_2[4]));  // open: en
  // Probe on bit_extender_4_out
  Negator #(.width(4)) negator_1 (.in(subtractor_1_out), .out(negator_1_out));
  assign bit_extender_4_out = {{1{1'b0}}, negator_1_out};  // Bit_Extender bit_extender_4
  Multiplexer #(.width(32)) multiplexer_3 (
    .in0(multiplexer_2_out), .in1({32{1'b0}}), .out(out_3), .sel(comparator_1_eq));  // open: en
endmodule
