// Logisim project P0_L1_navigation_2020.circ as structural Verilog: 2 circuits, main circuit navigation
module navigation (
  input  [1:0] dir,
  input  clk,
  input  reset,
  output arrive,
  output hit
);

  wire [2:0] status;
  wire [3:0] shift_1_s0_2;

  // Probe on {hit, status}
  shift shift_1 (
    .in1(dir[1]), .in0(dir[0]), .s2(status[2]), .s1(status[1]), .s0(status[0]), .h(hit),
    .s2_2(shift_1_s0_2[2]), .s1_2(shift_1_s0_2[1]), .s0_2(shift_1_s0_2[0]), .h_2(shift_1_s0_2[3]));
  Register #(.width(4)) register_1 (.D(shift_1_s0_2), .Q({hit, status}), .clk(clk), .clr(reset));  // open: en
  Comparator #(.width(3)) comparator_1 (.a(3'b100), .b(status), .eq(arrive));  // open: gt, lt

  // Other names for the same wires on the sheet: status[3] = hit
endmodule

module shift (
  input  in1,
  input  in0,
  input  s2,
  input  s1,
  input  s0,
  input  h,
  output s2_2,
  output s1_2,
  output s0_2,
  output h_2
);

  wire and_1_out, and_2_out, and_3_out, and_4_out, and_5_out, and_6_out, and_7_out, and_8_out, and_9_out,
       and_10_out, and_11_out, and_12_out, and_13_out, and_14_out, and_15_out, and_16_out, and_17_out,
       not_1_out, not_2_out, not_3_out, not_4_out, not_5_out, not_6_out, not_7_out, not_8_out, not_9_out,
       not_10_out, not_11_out, not_12_out, not_13_out, not_14_out, not_15_out, not_16_out, not_17_out,
       not_18_out, not_19_out, not_20_out, not_21_out, not_22_out, not_23_out, not_24_out, not_25_out,
       not_26_out, not_27_out, not_28_out, not_29_out, not_30_out, not_31_out, not_32_out, not_33_out,
       not_34_out, not_35_out, not_36_out, not_37_out, not_38_out, not_39_out, not_40_out, not_41_out,
       not_42_out, not_43_out, not_44_out, not_45_out;

  not not_1 (not_1_out, in1);
  not not_2 (not_2_out, in0);
  not not_3 (not_3_out, s2);
  not not_4 (not_4_out, in1);
  not not_5 (not_5_out, s2);
  not not_6 (not_6_out, s0);
  not not_7 (not_7_out, in1);
  not not_8 (not_8_out, s2);
  not not_9 (not_9_out, s1);
  not not_10 (not_10_out, in1);
  not not_11 (not_11_out, in0);
  not not_12 (not_12_out, s2);
  not not_13 (not_13_out, s0);
  not not_14 (not_14_out, in1);
  not not_15 (not_15_out, s2);
  not not_16 (not_16_out, in0);
  not not_17 (not_17_out, s2);
  not not_18 (not_18_out, s2);
  not not_19 (not_19_out, s0);
  not not_20 (not_20_out, in1);
  not not_21 (not_21_out, in0);
  not not_22 (not_22_out, s2);
  not not_23 (not_23_out, s1);
  not not_24 (not_24_out, s0);
  not not_25 (not_25_out, s2);
  not not_26 (not_26_out, in0);
  not not_27 (not_27_out, s2);
  not not_28 (not_28_out, in1);
  not not_29 (not_29_out, in0);
  not not_30 (not_30_out, s2);
  not not_31 (not_31_out, s0);
  not not_32 (not_32_out, s2);
  not not_33 (not_33_out, s1);
  not not_34 (not_34_out, s0);
  not not_35 (not_35_out, in1);
  not not_36 (not_36_out, s2);
  not not_37 (not_37_out, s2);
  not not_38 (not_38_out, s1);
  not not_39 (not_39_out, s0);
  not not_40 (not_40_out, in0);
  not not_41 (not_41_out, s2);
  not not_42 (not_42_out, s2);
  not not_43 (not_43_out, s1);
  not not_44 (not_44_out, s2);
  not not_45 (not_45_out, s0);
  and and_1 (and_1_out, not_1_out, not_2_out, not_3_out, s1, s0);
  and and_2 (and_2_out, not_4_out, in0, not_5_out, s1, not_6_out);
  and and_3 (and_3_out, not_7_out, not_8_out, not_9_out, s0);
  and and_4 (and_4_out, not_10_out, not_11_out, not_12_out, s1, not_13_out);
  and and_5 (and_5_out, not_14_out, in0, not_15_out, s0);
  and and_6 (and_6_out, in1, not_16_out, not_17_out, s1, s0);
  and and_7 (and_7_out, in1, in0, not_18_out, s1, not_19_out);
  and and_8 (and_8_out, not_20_out, not_21_out, not_22_out, not_23_out, not_24_out);
  and and_9 (and_9_out, in0, not_25_out, s0);
  and and_10 (and_10_out, in1, not_26_out, not_27_out, s1);
  and and_11 (and_11_out, not_28_out, not_29_out, not_30_out, s1, not_31_out);
  and and_12 (and_12_out, in0, not_32_out, not_33_out, not_34_out);
  and and_13 (and_13_out, not_35_out, in0, not_36_out, s1, s0);
  and and_14 (and_14_out, in1, not_37_out, not_38_out, not_39_out);
  and and_15 (and_15_out, in1, not_40_out, not_41_out, s1, s0);
  and and_16 (and_16_out, in1, in0, not_42_out, not_43_out);
  and and_17 (and_17_out, in1, in0, not_44_out, not_45_out);
  or or_1 (s2_2, and_1_out, and_2_out);
  or or_2 (s1_2, and_3_out, and_4_out, and_5_out, and_6_out, and_7_out);
  or or_3 (s0_2, and_8_out, and_9_out, and_10_out);
  or or_4 (h_2, and_11_out, and_12_out, and_13_out, and_14_out, and_15_out, and_16_out, and_17_out);
endmodule
