// Logisim project P0_L1_navigation_2020_2.circ as structural Verilog: 4 circuits, main circuit navigation
module navigation (
  input  [1:0] in_1,
  input  CLK,
  input  CLR,
  output ARR,
  output HIT
);

  wire reg_1_out_6, reg_1_out_7, reg_1_out_8, tran_1_hit, tran_1_o00, tran_1_o11, tran_1_o22;

  TRAN tran_1 (
    .O0(reg_1_out_6), .O1(reg_1_out_7), .O2(reg_1_out_8), .I0(in_1[1]), .I1(in_1[0]), .arr(ARR),
    .hit(tran_1_hit), .O00(tran_1_o00), .O11(tran_1_o11), .O22(tran_1_o22));
  REG reg_1 (
    .in_3(tran_1_o00), .in_4(tran_1_o11), .in_5(tran_1_o22), .CLK(CLK), .CLR(CLR), .out_6(reg_1_out_6),
    .out_7(reg_1_out_7), .out_8(reg_1_out_8));
  Register #(.width(1)) register_1 (.D(tran_1_hit), .Q(HIT), .clk(CLK), .clr(CLR));  // open: en
endmodule

module TRAN (
  input  O0,
  input  O1,
  input  O2,
  input  I0,
  input  I1,
  output O00,
  output O11,
  output O22,
  output arr,
  output hit
);

  wire and_1_out, and_2_out, and_3_out, and_4_out, and_5_out, and_6_out, and_7_out, and_8_out, and_9_out,
       and_10_out, and_11_out, and_12_out, and_13_out, and_14_out, and_15_out, and_16_out, and_17_out,
       and_18_out, and_19_out, and_20_out, and_21_out, not_1_out, not_2_out, not_3_out, not_4_out, not_5_out,
       not_6_out, not_7_out, not_8_out, not_9_out, not_10_out, not_11_out, not_12_out, not_13_out,
       not_14_out, not_15_out, not_16_out, not_17_out, not_18_out, not_19_out, not_20_out, not_21_out,
       not_22_out, not_23_out, not_24_out, not_25_out;

  not not_1 (not_1_out, O2);
  not not_2 (not_2_out, I0);
  not not_3 (not_3_out, I1);
  not not_4 (not_4_out, I0);
  not not_5 (not_5_out, O1);
  not not_6 (not_6_out, I0);
  not not_7 (not_7_out, I0);
  not not_8 (not_8_out, I1);
  not not_9 (not_9_out, O2);
  not not_10 (not_10_out, I0);
  not not_11 (not_11_out, O2);
  not not_12 (not_12_out, I1);
  not not_13 (not_13_out, O0);
  not not_14 (not_14_out, O1);
  not not_15 (not_15_out, I0);
  not not_16 (not_16_out, I1);
  not not_17 (not_17_out, I1);
  not not_18 (not_18_out, O2);
  not not_19 (not_19_out, I0);
  not not_20 (not_20_out, O1);
  not not_21 (not_21_out, O2);
  not not_22 (not_22_out, O2);
  not not_23 (not_23_out, I1);
  not not_24 (not_24_out, I0);
  not not_25 (not_25_out, I1);
  and and_1 (and_1_out, O1, not_1_out, not_2_out, not_3_out);
  and and_2 (and_2_out, O1, O2, not_4_out, I1);
  and and_3 (and_3_out, O0, O1);
  and and_4 (and_4_out, not_5_out, O2, not_6_out);
  and and_5 (and_5_out, O2, not_7_out, not_8_out);
  and and_6 (and_6_out, O1, not_9_out, not_10_out, I1);
  and and_7 (and_7_out, O1, not_11_out, I0, not_12_out);
  and and_8 (and_8_out, O1, O2, I0, I1);
  and and_9 (and_9_out, O0, O2);
  and and_10 (and_10_out, not_13_out, not_14_out, not_15_out, not_16_out);
  and and_11 (and_11_out, O2, I0, I1);
  and and_12 (and_12_out, O1, I0, I1);
  and and_13 (and_13_out, O1, O2, not_17_out);
  and and_14 (and_14_out, O0, O2);
  and and_15 (and_15_out, O0, O1);
  and and_16 (and_16_out, not_18_out, not_19_out, I1);
  and and_17 (and_17_out, not_20_out, not_21_out, I0);
  and and_18 (and_18_out, not_22_out, I0, not_23_out);
  and and_19 (and_19_out, O2, I0, I1);
  and and_20 (and_20_out, O1, O2, not_24_out, not_25_out);
  and and_21 (and_21_out, O0, O1);
  or or_1 (O00, and_1_out, and_2_out, and_3_out);
  or or_2 (O11, and_4_out, and_5_out, and_6_out, and_7_out, and_8_out, and_9_out);
  or or_3 (O22, and_10_out, and_11_out, and_12_out, and_13_out, and_14_out, and_15_out);
  or or_4 (hit, and_16_out, and_17_out, and_18_out, and_19_out, and_20_out, and_21_out);

  assign arr = O0;
endmodule

module REG (
  input  CLK,
  input  CLR,
  input  in_3,
  input  in_4,
  input  in_5,
  output out_6,
  output out_7,
  output out_8
);

  wire not_1_out, not_2_out, not_3_out, register_1_q, register_2_q, register_3_q;

  Register #(.width(1)) register_1 (.D(CLR), .Q(register_1_q), .clk(CLK), .clr(not_1_out));  // open: en
  not not_1 (not_1_out, CLR);
  Register #(.width(1)) register_2 (.D(CLR), .Q(register_2_q), .clk(CLK), .clr(not_2_out));  // open: en
  not not_2 (not_2_out, CLR);
  Register #(.width(1)) register_3 (.D(CLR), .Q(register_3_q), .clk(CLK), .clr(not_3_out));  // open: en
  not not_3 (not_3_out, CLR);
  Register #(.width(1)) register_4 (.D(in_3), .Q(out_6), .clk(CLK), .clr(register_1_q));  // open: en
  Register #(.width(1)) register_5 (.D(in_4), .Q(out_7), .clk(CLK), .clr(register_2_q));  // open: en
  Register #(.width(1)) register_6 (.D(in_5), .Q(out_8), .clk(CLK), .clr(register_3_q));  // open: en
endmodule

module OUT_ARR (
  input  O0,
  input  O1,
  input  O2,
  input  I0,
  input  I1,
  output ARRIVE,
  output HIT
);

  wire and_1_out, and_2_out, and_3_out, and_4_out, and_5_out, and_6_out, and_7_out, and_8_out, not_1_out,
       not_2_out, not_3_out, not_4_out, not_5_out, not_6_out, not_7_out, not_8_out, not_9_out, not_10_out,
       not_11_out, not_12_out, not_13_out, not_14_out;

  not not_1 (not_1_out, O0);
  not not_2 (not_2_out, O1);
  not not_3 (not_3_out, O2);
  not not_4 (not_4_out, O0);
  not not_5 (not_5_out, O2);
  not not_6 (not_6_out, I0);
  not not_7 (not_7_out, O0);
  not not_8 (not_8_out, O2);
  not not_9 (not_9_out, I1);
  not not_10 (not_10_out, I0);
  not not_11 (not_11_out, I1);
  not not_12 (not_12_out, I0);
  not not_13 (not_13_out, I0);
  not not_14 (not_14_out, I0);
  and and_1 (and_1_out, not_1_out, not_2_out, not_3_out, I1);
  and and_2 (and_2_out, not_4_out, not_5_out, not_6_out, I1);
  and and_3 (and_3_out, not_7_out, not_8_out, I0, not_9_out);
  and and_4 (and_4_out, O2, I0, I1);
  and and_5 (and_5_out, O1, O2, not_10_out, not_11_out);
  and and_6 (and_6_out, O0, O2, not_12_out);
  and and_7 (and_7_out, O0, O1, not_13_out);
  and and_8 (and_8_out, ARRIVE, O0, not_14_out);
  or or_1 (HIT, and_1_out, and_2_out, and_3_out, and_4_out, and_5_out, and_6_out, and_7_out, and_8_out);
endmodule
