// Logisim project P3_CPU.circ as structural Verilog: 8 circuits, main circuit grf
// GRF
module grf (
  input  [4:0] A1,
  input  [4:0] A2,
  input  reset,
  input  clk,
  input  [31:0] WD,
  input  [4:0] A3,
  input  WE,
  output [31:0] RD1,
  output [31:0] RD2
);

  wire [4:0] and_1_out, bit_extender_1_out;
  wire [31:0] _0, _1, _2, _3, _4, _5, _6, _7, _8, _9, _10, _11, _12, _13, _14, _15, _16, _17, _18, _19, _20,
       _21, _22, _23, _24, _25, _26, _27, _28, _29, _30, _31, WD0, WD1, WD2, WD3, WD4, WD5, WD6, WD7, WD8,
       WD9, WD10, WD11, WD12, WD13, WD14, WD15, WD16, WD17, WD18, WD19, WD20, WD21, WD22, WD23, WD24, WD25,
       WD26, WD27, WD28, WD29, WD30, WD31;

  assign bit_extender_1_out = {{4{WE}}, WE};  // Bit_Extender bit_extender_1
  Register #(.width(32)) register_1 (.D(WD0), .Q(_0), .clk(clk), .clr(reset));  // open: en
  Register #(.width(32)) register_2 (.D(WD8), .Q(_8), .clk(clk), .clr(reset));  // open: en
  Register #(.width(32)) register_3 (.D(WD16), .Q(_16), .clk(clk), .clr(reset));  // open: en
  Register #(.width(32)) register_4 (.D(WD24), .Q(_24), .clk(clk), .clr(reset));  // open: en
  // Probe on and_1_out
  assign and_1_out = A3 & bit_extender_1_out;  // AND_Gate and_1, 5 bits wide
  // Probe on WD1
  Demultiplexer #(.select(5), .width(32), .tristate("true")) demultiplexer_1 (
    .out1(WD1), .out2(WD2), .out3(WD3), .out4(WD4), .out5(WD5), .out6(WD6), .out7(WD7), .out8(WD8),
    .out9(WD9), .out10(WD10), .out11(WD11), .out12(WD12), .out13(WD13), .out14(WD14), .out15(WD15),
    .out16(WD16), .out17(WD17), .out18(WD18), .out19(WD19), .out20(WD20), .out21(WD21), .out22(WD22),
    .out23(WD23), .out24(WD24), .out25(WD25), .out26(WD26), .out27(WD27), .out28(WD28), .out29(WD29),
    .out30(WD30), .out31(WD31), .in(WD), .sel(and_1_out));  // open: out0, en
  Register #(.width(32)) register_5 (.D(WD1), .Q(_1), .clk(clk), .clr(reset));  // open: en
  Register #(.width(32)) register_6 (.D(WD9), .Q(_9), .clk(clk), .clr(reset));  // open: en
  Register #(.width(32)) register_7 (.D(WD17), .Q(_17), .clk(clk), .clr(reset));  // open: en
  Register #(.width(32)) register_8 (.D(WD25), .Q(_25), .clk(clk), .clr(reset));  // open: en
  Register #(.width(32)) register_9 (.D(WD2), .Q(_2), .clk(clk), .clr(reset));  // open: en
  Register #(.width(32)) register_10 (.D(WD10), .Q(_10), .clk(clk), .clr(reset));  // open: en
  Register #(.width(32)) register_11 (.D(WD18), .Q(_18), .clk(clk), .clr(reset));  // open: en
  Register #(.width(32)) register_12 (.D(WD26), .Q(_26), .clk(clk), .clr(reset));  // open: en
  Register #(.width(32)) register_13 (.D(WD3), .Q(_3), .clk(clk), .clr(reset));  // open: en
  Register #(.width(32)) register_14 (.D(WD11), .Q(_11), .clk(clk), .clr(reset));  // open: en
  Register #(.width(32)) register_15 (.D(WD19), .Q(_19), .clk(clk), .clr(reset));  // open: en
  Register #(.width(32)) register_16 (.D(WD27), .Q(_27), .clk(clk), .clr(reset));  // open: en
  Register #(.width(32)) register_17 (.D(WD4), .Q(_4), .clk(clk), .clr(reset));  // open: en
  Register #(.width(32)) register_18 (.D(WD12), .Q(_12), .clk(clk), .clr(reset));  // open: en
  Register #(.width(32)) register_19 (.D(WD20), .Q(_20), .clk(clk), .clr(reset));  // open: en
  Register #(.width(32)) register_20 (.D(WD28), .Q(_28), .clk(clk), .clr(reset));  // open: en
  // Probe on _0
  Register #(.width(32)) register_21 (.D(WD5), .Q(_5), .clk(clk), .clr(reset));  // open: en
  Register #(.width(32)) register_22 (.D(WD13), .Q(_13), .clk(clk), .clr(reset));  // open: en
  Register #(.width(32)) register_23 (.D(WD21), .Q(_21), .clk(clk), .clr(reset));  // open: en
  Register #(.width(32)) register_24 (.D(WD29), .Q(_29), .clk(clk), .clr(reset));  // open: en
  Register #(.width(32)) register_25 (.D(WD6), .Q(_6), .clk(clk), .clr(reset));  // open: en
  Register #(.width(32)) register_26 (.D(WD14), .Q(_14), .clk(clk), .clr(reset));  // open: en
  Register #(.width(32)) register_27 (.D(WD22), .Q(_22), .clk(clk), .clr(reset));  // open: en
  Register #(.width(32)) register_28 (.D(WD30), .Q(_30), .clk(clk), .clr(reset));  // open: en
  Multiplexer #(.select(5), .width(32)) multiplexer_1 (
    .in0(_0), .in1(_1), .in2(_2), .in3(_3), .in4(_4), .in5(_5), .in6(_6), .in7(_7), .in8(_8), .in9(_9),
    .in10(_10), .in11(_11), .in12(_12), .in13(_13), .in14(_14), .in15(_15), .in16(_16), .in17(_17),
    .in18(_18), .in19(_19), .in20(_20), .in21(_21), .in22(_22), .in23(_23), .in24(_24), .in25(_25),
    .in26(_26), .in27(_27), .in28(_28), .in29(_29), .in30(_30), .in31(_31), .out(RD2), .sel(A2));  // open: en
  Register #(.width(32)) register_29 (.D(WD7), .Q(_7), .clk(clk), .clr(reset));  // open: en
  Register #(.width(32)) register_30 (.D(WD15), .Q(_15), .clk(clk), .clr(reset));  // open: en
  Register #(.width(32)) register_31 (.D(WD23), .Q(_23), .clk(clk), .clr(reset));  // open: en
  Register #(.width(32)) register_32 (.D(WD31), .Q(_31), .clk(clk), .clr(reset));  // open: en
  // Probe on _0
  Multiplexer #(.select(5), .width(32)) multiplexer_2 (
    .in0(_0), .in1(_1), .in2(_2), .in3(_3), .in4(_4), .in5(_5), .in6(_6), .in7(_7), .in8(_8), .in9(_9),
    .in10(_10), .in11(_11), .in12(_12), .in13(_13), .in14(_14), .in15(_15), .in16(_16), .in17(_17),
    .in18(_18), .in19(_19), .in20(_20), .in21(_21), .in22(_22), .in23(_23), .in24(_24), .in25(_25),
    .in26(_26), .in27(_27), .in28(_28), .in29(_29), .in30(_30), .in31(_31), .out(RD1), .sel(A1));  // open: en

  // Other names for the same wires on the sheet: d1[31:0] = RD1; d2[31:0] = RD2
endmodule

module enable (
  input  [31:0] in_1,
  input  [4:0] in_2,
  input  in_3
);

  wire [4:0] and_1_out, bit_extender_1_out;
  wire [31:0] WD1, WD2, WD3, WD4, WD5, WD6, WD7, WD8, WD9, WD10, WD11, WD12, WD13, WD14, WD15, WD16, WD17,
       WD18, WD19, WD20, WD21, WD22, WD23, WD24, WD25, WD26, WD27, WD28, WD29, WD30, WD31;

  assign bit_extender_1_out = {{4{in_3}}, in_3};  // Bit_Extender bit_extender_1
  assign and_1_out = in_2 & bit_extender_1_out;  // AND_Gate and_1, 5 bits wide
  // Probe on and_1_out
  Demultiplexer #(.select(5), .width(32)) demultiplexer_1 (
    .out1(WD1), .out2(WD2), .out3(WD3), .out4(WD4), .out5(WD5), .out6(WD6), .out7(WD7), .out8(WD8),
    .out9(WD9), .out10(WD10), .out11(WD11), .out12(WD12), .out13(WD13), .out14(WD14), .out15(WD15),
    .out16(WD16), .out17(WD17), .out18(WD18), .out19(WD19), .out20(WD20), .out21(WD21), .out22(WD22),
    .out23(WD23), .out24(WD24), .out25(WD25), .out26(WD26), .out27(WD27), .out28(WD28), .out29(WD29),
    .out30(WD30), .out31(WD31), .in(in_1), .sel(and_1_out));  // open: out0, en
endmodule

module out1 (
  input  [4:0] in_1,
  output [31:0] out_2
);

  wire [31:0] _0, _1, _2, _3, _4, _5, _6, _7, _8, _9, _10, _11, _12, _13, _14, _15, _16, _17, _18, _19, _20,
       _21, _22, _23, _24, _25, _26, _27, _28, _29, _30, _31;

  Multiplexer #(.select(5), .width(32)) multiplexer_1 (
    .in0(_0), .in1(_1), .in2(_2), .in3(_3), .in4(_4), .in5(_5), .in6(_6), .in7(_7), .in8(_8), .in9(_9),
    .in10(_10), .in11(_11), .in12(_12), .in13(_13), .in14(_14), .in15(_15), .in16(_16), .in17(_17),
    .in18(_18), .in19(_19), .in20(_20), .in21(_21), .in22(_22), .in23(_23), .in24(_24), .in25(_25),
    .in26(_26), .in27(_27), .in28(_28), .in29(_29), .in30(_30), .in31(_31), .out(out_2), .sel(in_1));  // open: en
endmodule

module main (
  input  reset,
  output [31:0] Instr,
  output [31:0] pc,
  output RegWrite,
  output [4:0] RegAddr,
  output [31:0] RegData,
  output MemWrite,
  output [31:0] MenAddr,
  output [31:0] MenData
);

  wire ALUSrc, and_1_out, bit_extender_2_out, clk, MentoReg, PCsel, RegDst;
  wire [1:0] Extop, PCop;
  wire [3:0] ALUop;
  wire [23:0] bit_extender_1_out, bit_extender_3_out, shifter_1_out, shifter_2_out;
  wire [31:0] beq, DMans, GRF_rd1, multiplexer_3_out, PC_t, PCshift_out_4;

  PCshift PCshift (.in_1(PCop), .beq(beq), .PC(PC_t), .out_4(PCshift_out_4));
  // Probe on PCshift_out_4
  Bit_Extender #(.in_width(32), .out_width(24)) bit_extender_1 (.in(PC_t), .out(bit_extender_1_out));
  Register #(.width(32)) register_1 (.D(PCshift_out_4), .Q(PC_t), .clk(clk), .clr(reset));  // open: en
  Shifter #(.width(24), .shift("lr")) shifter_1 (.in(bit_extender_1_out), .\dist (5'b00010), .out(shifter_1_out));
  ROM #(.addrWidth(24), .dataWidth(32)) rom_1 (.addr(shifter_1_out), .data(Instr));  // open: sel
  CU cu_1 (
    .op(Instr[31:26]), .func(Instr[5:0]), .RegDst(RegDst), .ALUSrc(ALUSrc), .MemtoReg(MentoReg),
    .Regwrite(RegWrite), .Memwrite(MemWrite), .PCsel(PCsel), .Extop(Extop), .ALUop(ALUop));
  Multiplexer #(.width(5)) multiplexer_1 (
    .in0(Instr[20:16]), .in1(Instr[15:11]), .out(RegAddr), .sel(RegDst));  // open: en
  Multiplexer #(.width(32)) multiplexer_2 (.in0(MenAddr), .in1(DMans), .out(RegData), .sel(MentoReg));  // open: en
  grf GRF (
    .clk(clk), .reset(reset), .WE(RegWrite), .A1(Instr[25:21]), .A2(Instr[20:16]), .A3(RegAddr),
    .WD(RegData), .RD1(GRF_rd1), .RD2(MenData));
  Clock clock_1 (.out(clk));
  Multiplexer #(.width(32)) multiplexer_3 (
    .in0(MenData), .in1(beq), .out(multiplexer_3_out), .sel(ALUSrc));  // open: en
  Extender extender_1 (.num(Instr[15:0]), .Extop(Extop), .ans(beq));
  ALU alu_1 (.num1(GRF_rd1), .num2(multiplexer_3_out), .ALUop(ALUop), .ans(MenAddr));
  // Probe on Instr
  // Probe on Instr[31:26]
  // Probe on Instr[5:0]
  Bit_Extender #(.in_width(32), .out_width(1)) bit_extender_2 (.in(MenAddr), .out(bit_extender_2_out));
  Bit_Extender #(.in_width(32), .out_width(24)) bit_extender_3 (.in(MenAddr), .out(bit_extender_3_out));
  and and_1 (and_1_out, bit_extender_2_out, PCsel);
  assign PCop = {{1{1'b0}}, and_1_out};  // Bit_Extender bit_extender_4
  Shifter #(.width(24), .shift("lr")) shifter_2 (.in(bit_extender_3_out), .\dist (5'b00010), .out(shifter_2_out));
  RAM #(.addrWidth(24), .dataWidth(32), .bus("separate")) ram_1 (
    .addr(shifter_2_out), .din(MenData), .data(DMans), .str(MemWrite), .clk(clk), .ld(MentoReg), .clr(reset));  // open: sel
  Adder #(.width(32)) adder_1 (.a(PC_t), .b(32'h3000), .out(pc));  // open: cin, cout

  // Other names for the same wires on the sheet: ALUans[31:0] = MenAddr; Func[5:0] = Instr[5:0];
  //   funcprobe[5:0] = Instr[5:0]; immediate[15:0] = Instr[15:0]; insprobe[31:0] = Instr; instruction[31:0] = Instr;
  //   Menwrite = MemWrite; Op[5:0] = Instr[31:26]; Oppreobe[5:0] = Instr[31:26]; rd[4:0] = Instr[15:11];
  //   rs[4:0] = Instr[25:21]; rt[4:0] = Instr[20:16]

  // Notes on the sheet:
  //   contents of rom_1 (hex, n*v repeats v):
  //   3c190ea6 f56022 3c0aa289 8c190600 356bd7cc 1171fffd 0 16aa820 274d020 3c177397 1973022 8c0c0f44
  //   35ca2de1 356b5a76 1176fff4 0 ac0c10ac ac0721cc 3c06dc24 1d38020 3487c86d 8c0e0d70 10f4820 28c4022
  //   4*0 372d820 e5d822 6e8020 17aa822 132d822 3721020 cb7820 12a4822 36b43bfe 352994cb 112effdd ac180d6c
  //   ac041c8c 8c031148 8c1b0a20 3c033cda 36b54a3f 12b9ffd5 34c6d00e 10d7ffd4 3c0aedc8 3c0caa72 3c06be7e 0
  //   0 ac09061c 3c094372 0 8c100c60 0 2ac8020 8c0a199c ac1a1cb0 2431822 34a5e0a9 10b5ffd3 3c0c12ad
  //   8c142d08 8c1726e0 3718d22d 130dfffd 35292a76 1128ffd0 8c0a2ecc 0 299b022 3c1a54cb 0 2493822 372b9abc
  //   8c09020c 129c022 3c10f35e 1305020 8c101548 36b54e0f 12b3ffed ac1211a8 ac100abc 0 ac1024b4 3c17074f
  //   26e6022 8c112fa0 8c142280 3c14a342 689822 2701822 36d6ee4d 12d2ffe0 ac131e94 36104bd9 121affb9
  //   3c16f27f ac090d7c 0 348c020 3c0bd1ac 8c0227ac 3694d8bf 128fff97 3c0c5597 2eaa822 ac0b2320 14cb020
  //   36940462 1286ffa4 3c08699e 35ce50d1 11caffc7 0 3c167980 0 b6b820 2282020 c37822 18f2020 3c10671a
  //   28b7820 3508e59c 1115ff96 345518e5 37244796 114c022 0 8c16020c 3c0bea70 0 d12020 ac0812cc ac0d0c74 0
  //   ac16164c 3c0ada5b 3c188477 0 ac0721d4 2b77822 0 34a53ffa 10baffd8 0 0 0 36516857 2da9820 1628822
  //   3164822 3c16c3a6 0 1cd2022 377b56b0 1378ff62 3c1b47a5 0 377ba117 1371ffb4 35291119 112effc3 3c03b8d0
  //   3647ce9e 35efda0e 11e5fffc 36adb2b2 3484a04d 108dff70 32bb020 368f77f9 ac1206b4 ac1806b8 3c199cc0
  //   1276020 0 8c122474 36f7ba85 12f0ff8a 36c647f0 8c131784 ac1a2e0c ac082170 0 35f774cf 188a822 377b62f0
  //   1368ffb9 ac090078 8c032990 248c820 8c192f0c ac18109c f42820 3463a32a 106dff74 34add4ef 3c02de26
  //   8c182e38 3664020 354a5f8e 1150ff8c 303a022 ac151bd0 3c093e3b 8c112344 ac04279c 8c1a169c 1868820
  //   172d022 8c1218bc 3c0cda07 14f2820 8c0d0784 364f2875 356b2951 117bffc9 36d61887 12d2fff8 8c0e14e4
  //   365c822 1029020 358358b4 0 305a822 19ba020 2c4d822 ac0d2b4c 34d5c287 367338ed 1269ffcf 26c1822
  //   1e73820 0 20e6820 3c0b8bf9 8c0d1168 375aac14 134effdb ac0312ec 2f62022 2dbc822 8c021468 8c132ca8 0
  //   2549020 8c0a2ce0 ac17109c 2181020 4e2022 0 ac101590 3c0d2c53 3c14221f 1c86820 ac0f09d8 344e4d82
  //   ac0a19e0 34f36142 34cc4927 8c09032c 3610f14d 1203ff4f 8c180b00 358ceafe 1185ff6b ac0e272c ac06007c
  //   34b977df 0 8c1b26e4 0 18c4020 358cb8c0 1194feeb ac0427c8 361085cc 1214fefc 8c121938 0 34842f5b
  //   1085ff7e ac1302a0 1539022 2b49022 ac131374 34e73ffe 8c181204 36d69a46 ac0c06f4 356bb76c 8c082a70 0
  //   177d022 358f24ef 3c032401 377b6907 1365ff2c 376372c4 0 364fe1f4 1724822 8c1909ac 3743b165 3c0be49e 0
  //   3c1b2b6a 8c071e70 1449820 26a7820 3c159bae 3738cff3 8c0b2844 2c8b822 8c181df0 0 346c020 36730c30
  //   126fffdc 3c1b3e06 ac03275c 8c191cdc 0 377b1ee4 1369ff8e 2cc9022 3285022 ac16241c 3442b939 1052ff1a
  //   1519822 14db020 74d020 ac0718b4 0 718822 ac0c1cdc 1c68022 d35822 352c8fa1 3c0dfb6a ac1512b8 3729e2e3
  //   35adf0c4 11a4ffd6 3c0ca376 3c1179cd ac0b20a0 12c5822 8c160b68 34aaa700 ac1a0b20 8c1a2b2c 8c101cbc
  //   ac0a2cc0 8c0308d8 3c11e554 ac1229c4 3c18d7db 8c062894 0 34c27f56 2b07820 0 3166820 ac0f0de8 36ea0e66
  //   3673fda3 1271ff04 363153c1 1225ffac 36f735bf 12f5fff8 34e701bd 3694921c 1290fe87 0 8c042e78 10f6822
  //   36d6dec8 12cdffbb 34a5b5f4 10bbffee 36d619e0 12c6fee4 35ade694 11b9ffa7 375a67c4 1353ff5c 0 ac160c94
  //   8c0e0254 3c12535c 3c085483 ac062ebc ac181c70 3c0731de 0 0 35294e23 1138ff50 2517022 e24022 f8d820
  //   ac1a21d4 8c071630 34843914 1092ff7f ac162178 3c0d1e83 361010b6 1204fec9 ac1602c4 ac1a2ed0 8c0d1bac
  //   ac181158 35ad0bf2 11b5ff3f 0 36edf917 ecc022 35ac648d 799822 8c0c2a00 34e7dd1a 10e3fef8 3c18cccf
  //   304d022 27a8820 2d61022 0 1115820 3c103ce1 8c1a0ec8 8c1222ec 3c053544 0 3032020 0 ac1a11bc 1ef6020
  //   ac0d14f4 ac1a2420 8c0b04ec ac1a1d70 36ab93b4 35075543 34425046 1046ff4a 8c032338 3442181e 1050fffb
  //   18fd822 0 8c132b6c 358c4e3a 1186ff0a 2759020 22bd022 36e7e603 8c082ef8 374d7a1f 3c036f16 ac082708
  //   3c12f044 3c064404 8c0e2c0c 3c0b4003 1da9820 ac18296c ac072718 34e7e787 10ecfefa 8c1a217c 0 ac0d0970
  //   0 35b9f3eb 36ed09ab 0 0 37571c1f 1069020 1739020 3c075a5c ac1627c8 8c0e0ef4 ac052b74
endmodule

module PCshift (
  input  [1:0] in_1,
  input  [31:0] beq,
  input  [31:0] PC,
  output [31:0] out_4
);

  wire [31:0] _00, _01;

  // Probe on _01
  Adder #(.width(32)) adder_1 (.a(beq), .b(_00), .out(_01));  // open: cin, cout
  Adder #(.width(32)) adder_2 (.a(PC), .b(32'h4), .out(_00));  // open: cin, cout
  Multiplexer #(.select(2), .width(32)) multiplexer_1 (
    .in0(_00), .in1(_01), .out(out_4), .sel(in_1));  // open: in2, in3, en

  // Other names for the same wires on the sheet: PCop[1:0] = in_1
endmodule

module ALU (
  input  [31:0] num1,
  input  [31:0] num2,
  input  [3:0] ALUop,
  output [31:0] ans
);

  wire _0011, _0100, _0101;
  wire [31:0] _0000, _0001, _0010, _0110, bit_extender_1_out, bit_extender_2_out, bit_extender_3_out;

  Adder #(.width(32)) adder_1 (.a(num1), .b(num2), .out(_0000));  // open: cin, cout
  assign bit_extender_1_out = {{31{1'b0}}, _0011};  // Bit_Extender bit_extender_1
  assign bit_extender_2_out = {{31{1'b0}}, _0101};  // Bit_Extender bit_extender_2
  Subtractor #(.width(32)) subtractor_1 (.a(num1), .b(num2), .out(_0001));  // open: bin, bout
  assign bit_extender_3_out = {{31{1'b0}}, _0100};  // Bit_Extender bit_extender_3
  Multiplexer #(.select(4), .width(32)) multiplexer_1 (
    .in0(_0000), .in1(_0001), .in2(_0010), .in3(bit_extender_1_out), .in4(bit_extender_3_out),
    .in5(bit_extender_2_out), .in6(_0110), .out(ans), .sel(ALUop));  // open: in7, in8, in9, in10, in11, in12, in13, in14, in15, en
  assign _0010 = num1 | num2;  // OR_Gate or_1, 32 bits wide
  Comparator #(.width(32)) comparator_1 (.a(num1), .b(num2), .gt(_0101), .eq(_0011), .lt(_0100));
  assign _0110 = num1 & num2;  // AND_Gate and_1, 32 bits wide

  // Other names for the same wires on the sheet: op[3:0] = ALUop
endmodule

module CU (
  input  [5:0] op,
  input  [5:0] func,
  output RegDst,
  output ALUSrc,
  output MemtoReg,
  output Regwrite,
  output Memwrite,
  output PCsel,
  output [1:0] Extop,
  output [3:0] ALUop
);

  wire add, add_out, and2, beq, j, lui, lw, or_1_out, or_2_out, ori, sub, sub2, sub_out, sw;
  wire [1:0] and_3_out, and_4_out, and_5_out, and_6_out, bit_extender_1_out, bit_extender_2_out,
       bit_extender_3_out, bit_extender_4_out;
  wire [3:0] and_7_out, and_8_out, and_9_out, and_10_out, bit_extender_5_out, bit_extender_6_out,
       bit_extender_7_out, bit_extender_8_out;

  Comparator #(.width(6)) comparator_1 (.a(func), .b(6'b100000), .eq(and2));  // open: gt, lt
  Comparator #(.width(6)) comparator_2 (.a(func), .b(6'b100010), .eq(sub2));  // open: gt, lt
  and u_add (add_out, ~op[5], ~op[4], ~op[3], ~op[2], ~op[1], ~op[0]);  // AND_Gate
  and and_1 (add, add_out, and2);
  and u_sub (sub_out, ~op[5], ~op[4], ~op[3], ~op[2], ~op[1], ~op[0]);  // AND_Gate
  and and_2 (sub, sub_out, sub2);
  and u_ori (ori, ~op[5], ~op[4], op[3], op[2], ~op[1], op[0]);  // AND_Gate
  and u_lui (lui, ~op[5], ~op[4], op[3], op[2], op[1], op[0]);  // AND_Gate
  and u_lw (lw, op[5], ~op[4], ~op[3], ~op[2], op[1], op[0]);  // AND_Gate
  and u_sw (sw, op[5], ~op[4], op[3], ~op[2], op[1], op[0]);  // AND_Gate
  and u_beq (beq, ~op[5], ~op[4], ~op[3], op[2], ~op[1], ~op[0]);  // AND_Gate
  and u_j (j, ~op[5], ~op[4], ~op[3], ~op[2], op[1], ~op[0]);  // AND_Gate
  assign bit_extender_1_out = {{1{ori}}, ori};  // Bit_Extender bit_extender_1
  or or_1 (or_1_out, sw, lw);
  assign bit_extender_2_out = {{1{or_1_out}}, or_1_out};  // Bit_Extender bit_extender_2
  assign bit_extender_3_out = {{1{lui}}, lui};  // Bit_Extender bit_extender_3
  assign bit_extender_4_out = {{1{beq}}, beq};  // Bit_Extender bit_extender_4
  assign bit_extender_5_out = {{3{or_2_out}}, or_2_out};  // Bit_Extender bit_extender_5
  or or_2 (or_2_out, add, sw, lw);
  assign bit_extender_6_out = {{3{sub}}, sub};  // Bit_Extender bit_extender_6
  assign bit_extender_7_out = {{3{ori}}, ori};  // Bit_Extender bit_extender_7
  assign bit_extender_8_out = {{3{beq}}, beq};  // Bit_Extender bit_extender_8
  assign and_3_out = bit_extender_1_out & 2'b00;  // AND_Gate and_3, 2 bits wide
  assign and_4_out = bit_extender_2_out & 2'b01;  // AND_Gate and_4, 2 bits wide
  assign and_5_out = bit_extender_3_out & 2'b10;  // AND_Gate and_5, 2 bits wide
  assign and_6_out = bit_extender_4_out & 2'b11;  // AND_Gate and_6, 2 bits wide
  assign and_7_out = bit_extender_5_out & 4'b0000;  // AND_Gate and_7, 4 bits wide
  assign and_8_out = bit_extender_6_out & 4'b0001;  // AND_Gate and_8, 4 bits wide
  assign and_9_out = bit_extender_7_out & 4'b0010;  // AND_Gate and_9, 4 bits wide
  assign and_10_out = bit_extender_8_out & 4'b0011;  // AND_Gate and_10, 4 bits wide
  or or_3 (RegDst, add, sub);
  or or_4 (ALUSrc, ori, lw, sw, lui);
  buf or_5 (MemtoReg, lw);  // OR_Gate
  or or_6 (Regwrite, add, sub, ori, lw, lui);
  buf or_7 (Memwrite, sw);  // OR_Gate
  buf or_8 (PCsel, beq);  // OR_Gate
  assign Extop = and_3_out | and_4_out | and_5_out | and_6_out;  // OR_Gate or_9, 2 bits wide
  assign ALUop = and_7_out | and_8_out | and_9_out | and_10_out;  // OR_Gate or_10, 4 bits wide
endmodule

// Ext
module Extender (
  input  [15:0] num,
  input  [1:0] Extop,
  output [31:0] ans
);

  wire [31:0] _00, _01, _10, _11, bit_extender_3_out, bit_extender_4_out;

  assign _00 = {{16{1'b0}}, num};  // Bit_Extender bit_extender_1
  assign _01 = {{16{num[15]}}, num};  // Bit_Extender bit_extender_2
  assign bit_extender_3_out = {{16{1'b0}}, num};  // Bit_Extender bit_extender_3
  Shifter #(.width(32)) shifter_1 (.in(bit_extender_3_out), .\dist (5'b10000), .out(_10));
  assign bit_extender_4_out = {{16{num[15]}}, num};  // Bit_Extender bit_extender_4
  Shifter #(.width(32)) shifter_2 (.in(bit_extender_4_out), .\dist (5'b00010), .out(_11));
  Multiplexer #(.select(2), .width(32)) multiplexer_1 (
    .in0(_00), .in1(_01), .in2(_10), .in3(_11), .out(ans), .sel(Extop));  // open: en

  // Other names for the same wires on the sheet: op[1:0] = Extop
endmodule
