// Logisim project logisim_4BItSort.circ as structural Verilog: 3 circuits, main circuit 4bit_sort
module _4bit_sort (
  input  [3:0] A,
  input  [3:0] B,
  input  [3:0] C,
  input  [3:0] D,
  output [3:0] _1,
  output [3:0] _2,
  output [3:0] _3,
  output [3:0] _4
);

  wire comparator_1_gt, comparator_2_gt, comparator_3_gt, comparator_4_gt, comparator_5_gt, comparator_6_gt;
  wire [3:0] n4bit_swap_1__1, n4bit_swap_1__2, n4bit_swap_2__1, n4bit_swap_2__2, n4bit_swap_3__1,
       n4bit_swap_4__1, n4bit_swap_4__2, n4bit_swap_5__1;

  _4bit_swap u_4bit_swap_1 (.A(A), .B(B), .S(comparator_1_gt), ._1(n4bit_swap_1__1), ._2(n4bit_swap_1__2));
  Comparator #(.width(4), .mode("unsigned")) comparator_1 (.a(A), .b(B), .gt(comparator_1_gt));  // open: eq, lt
  _4bit_swap u_4bit_swap_2 (
    .A(n4bit_swap_1__2), .B(C), .S(comparator_2_gt), ._1(n4bit_swap_2__1), ._2(n4bit_swap_2__2));
  Comparator #(.width(4), .mode("unsigned")) comparator_2 (
    .a(n4bit_swap_1__2), .b(C), .gt(comparator_2_gt));  // open: eq, lt
  _4bit_swap u_4bit_swap_3 (.A(n4bit_swap_2__2), .B(D), .S(comparator_3_gt), ._1(n4bit_swap_3__1), ._2(_4));
  Comparator #(.width(4), .mode("unsigned")) comparator_3 (
    .a(n4bit_swap_2__2), .b(D), .gt(comparator_3_gt));  // open: eq, lt
  _4bit_swap u_4bit_swap_4 (
    .A(n4bit_swap_1__1), .B(n4bit_swap_2__1), .S(comparator_4_gt), ._1(n4bit_swap_4__1), ._2(n4bit_swap_4__2));
  Comparator #(.width(4), .mode("unsigned")) comparator_4 (
    .a(n4bit_swap_1__1), .b(n4bit_swap_2__1), .gt(comparator_4_gt));  // open: eq, lt
  _4bit_swap u_4bit_swap_5 (
    .A(n4bit_swap_4__2), .B(n4bit_swap_3__1), .S(comparator_5_gt), ._1(n4bit_swap_5__1), ._2(_3));
  Comparator #(.width(4)) comparator_5 (
    .a(n4bit_swap_4__2), .b(n4bit_swap_3__1), .gt(comparator_5_gt));  // open: eq, lt
  _4bit_swap u_4bit_swap_6 (.A(n4bit_swap_4__1), .B(n4bit_swap_5__1), .S(comparator_6_gt), ._1(_1), ._2(_2));
  Comparator #(.width(4), .mode("unsigned")) comparator_6 (
    .a(n4bit_swap_4__1), .b(n4bit_swap_5__1), .gt(comparator_6_gt));  // open: eq, lt
endmodule

module _1bit_swap (
  input  A,
  input  B,
  input  S,
  output _1,
  output _2
);

  wire and_1_out, and_2_out, and_3_out, and_4_out, not_1_out, not_2_out;

  not not_1 (not_1_out, S);
  not not_2 (not_2_out, S);
  and and_1 (and_1_out, A, not_1_out);
  and and_2 (and_2_out, B, S);
  and and_3 (and_3_out, A, S);
  and and_4 (and_4_out, B, not_2_out);
  or or_1 (_1, and_1_out, and_2_out);
  or or_2 (_2, and_3_out, and_4_out);
endmodule

module _4bit_swap (
  input  [3:0] A,
  input  [3:0] B,
  input  S,
  output [3:0] _1,
  output [3:0] _2
);

  _1bit_swap u_1bit_swap_1 (.A(A[0]), .B(B[0]), .S(S), ._1(_1[0]), ._2(_2[0]));
  _1bit_swap u_1bit_swap_2 (.A(A[1]), .B(B[1]), .S(S), ._1(_1[1]), ._2(_2[1]));
  _1bit_swap u_1bit_swap_3 (.A(A[2]), .B(B[2]), .S(S), ._1(_1[2]), ._2(_2[2]));
  _1bit_swap u_1bit_swap_4 (.A(A[3]), .B(B[3]), .S(S), ._1(_1[3]), ._2(_2[3]));
endmodule
