// Logisim project logisim_fibonacci_1.circ as structural Verilog: 2 circuits, main circuit main
module main (
  input  [2:0] N,
  output [3:0] Nth
);

  wire clock_1_out, comparator_1_eq, comparator_1_lt, comparator_2_lt, not_1_out;
  wire [3:0] adder_1_out, Fn_1_q, Fn_2_q, multiplexer_1_out, register_1_q, sub1_1_out_2;
  wire [7:0] bit_extender_1_out, counter_1_q, subtractor_1_out;

  // Probe on Fn_1_q
  Register #(.width(4)) Fn_1 (.D(adder_1_out), .Q(Fn_1_q), .clk(clock_1_out));  // open: en, clr
  // Probe on sub1_1_out_2
  sub1 sub1_1 (.in_1(Fn_1_q), .out_2(sub1_1_out_2));
  Clock clock_1 (.out(clock_1_out));
  // Probe on Fn_2_q
  Counter counter_1 (.Q(counter_1_q), .clk(clock_1_out));  // open: load, D, count, carry, clr
  Register #(.width(4)) Fn_2 (.D(sub1_1_out_2), .Q(Fn_2_q), .clk(clock_1_out));  // open: en, clr
  // Probe on adder_1_out
  Adder #(.width(4)) adder_1 (.a(Fn_2_q), .b(sub1_1_out_2), .out(adder_1_out));  // open: cin, cout
  assign bit_extender_1_out = {{5{1'b0}}, N};  // Bit_Extender bit_extender_1
  Subtractor subtractor_1 (.a(bit_extender_1_out), .b(8'h2), .out(subtractor_1_out));  // open: bin, bout
  Comparator comparator_1 (
    .a(subtractor_1_out), .b(counter_1_q), .eq(comparator_1_eq), .lt(comparator_1_lt));  // open: gt
  // Probe on multiplexer_1_out
  Multiplexer #(.width(4)) multiplexer_1 (
    .in0(4'b0000), .in1(adder_1_out), .out(multiplexer_1_out), .sel(comparator_1_eq));  // open: en
  Register #(.width(4)) register_1 (
    .D(multiplexer_1_out), .en(not_1_out), .Q(register_1_q), .clk(clock_1_out));  // open: clr
  not not_1 (not_1_out, comparator_1_lt);
  Multiplexer #(.width(4)) multiplexer_2 (
    .in0(register_1_q), .in1(4'b0001), .out(Nth), .sel(comparator_2_lt));  // open: en
  Comparator #(.width(3), .mode("unsigned")) comparator_2 (.a(N), .b(3'b010), .lt(comparator_2_lt));  // open: gt, eq

  // Other names for the same wires on the sheet: _1[2:0] = N

  // Notes on the sheet:
  //   Fn
endmodule

module sub1 (
  input  [3:0] in_1,
  output [3:0] out_2
);

  Multiplexer #(.select(4), .width(4)) multiplexer_1 (
    .in0(4'b0001), .in1(in_1), .in2(in_1), .in3(in_1), .in4(in_1), .in5(in_1), .in6(in_1), .in7(in_1),
    .in8(in_1), .in9(in_1), .in10(in_1), .in11(in_1), .in12(in_1), .in13(in_1), .in14(in_1), .in15(in_1),
    .out(out_2), .sel(in_1));  // open: en
endmodule
