// Logisim project logisim_full_adder.circ as structural Verilog: 2 circuits, main circuit main
module main (
  input  [3:0] in_1,
  input  [3:0] in_2,
  input  [3:0] in_3,
  input  [3:0] in_4,
  input  [3:0] in_5,
  input  [3:0] in_6,
  output [3:0] out_7,
  output [3:0] out_8
);

  Demultiplexer demultiplexer_1 ();  // open: out0, out1, in, sel, en
  Multiplexer multiplexer_1 ();  // open: in0, in1, out, sel, en
  ExactlyOne xor_1[3:0] (.out(out_7), .in1(in_1), .in2(in_2), .in3(in_3));
  assign out_8 = ~(in_4 ^ in_5 ^ in_6);  // XNOR_Gate xnor_1, 4 bits wide
  Decoder #(.select(3)) decoder_1 (.sel(3'b011));  // open: out0, out1, out2, out3, out4, out5, out6, out7, en
endmodule

module full_adder (
  input  a,
  input  b,
  input  carry,
  output carry_2,
  output sum
);

  wire and_1_out, and_2_out, and_3_out, and_4_out, and_5_out, and_6_out, and_7_out, not_1_out, not_2_out,
       not_3_out, not_4_out, not_5_out, not_6_out;

  and and_1 (and_1_out, b, carry);
  and and_2 (and_2_out, a, carry);
  and and_3 (and_3_out, a, b);
  not not_1 (not_1_out, a);
  not not_2 (not_2_out, b);
  not not_3 (not_3_out, a);
  not not_4 (not_4_out, carry);
  not not_5 (not_5_out, b);
  not not_6 (not_6_out, carry);
  or or_1 (carry_2, and_1_out, and_2_out, and_3_out);
  and and_4 (and_4_out, not_1_out, not_2_out, carry);
  and and_5 (and_5_out, not_3_out, b, not_4_out);
  and and_6 (and_6_out, a, not_5_out, not_6_out);
  and and_7 (and_7_out, a, b, carry);
  or or_2 (sum, and_4_out, and_5_out, and_6_out, and_7_out);
endmodule
