// Logisim project logisim_mod5.circ as structural Verilog: 1 circuit, main circuit mod5
module mod5 (
  input  In,
  output S0,
  output S1,
  output S2,
  output S3,
  output S4
);

  wire clock_1_out;
  wire [1:0] bit_extender_1_out, bitfinder_1_index;
  wire [2:0] multiplexer_2_out;
  wire [3:0] multiplexer_1_out, shifter_1_out, situation;

  // Probe on situation
  assign bit_extender_1_out = {{1{1'b0}}, In};  // Bit_Extender bit_extender_1
  Multiplexer #(.select(4), .width(4)) multiplexer_1 (
    .in0(4'b0001), .in1(4'b0001), .in2(4'b0100), .in4(4'b0001), .in8(4'b0100), .out(multiplexer_1_out),
    .sel(situation));  // open: in3, in5, in6, in7, in9, in10, in11, in12, in13, in14, in15, en
  // Probe on shifter_1_out
  Shifter #(.width(4), .shift("rl")) shifter_1 (
    .in(multiplexer_1_out), .\dist (bit_extender_1_out), .out(shifter_1_out));
  Clock clock_1 (.out(clock_1_out));
  // Probe on situation
  Register #(.width(4)) register_1 (.D(shifter_1_out), .Q(situation), .clk(clock_1_out));  // open: en, clr
  BitFinder #(.width(4)) bitfinder_1 (.in(situation), .index(bitfinder_1_index));  // open: found
  // Probe on bitfinder_1_index
  // Probe on multiplexer_2_out
  Multiplexer #(.select(2), .width(3)) multiplexer_2 (
    .in0(3'b001), .in1(3'b010), .in2(3'b100), .in3(3'b011), .out(multiplexer_2_out), .sel(bitfinder_1_index));  // open: en
  Decoder #(.select(3)) decoder_1 (
    .out0(S0), .out1(S1), .out2(S2), .out3(S3), .out4(S4), .sel(multiplexer_2_out));  // open: out5, out6, out7, en
endmodule
