// Logisim project logisim_mux.circ as structural Verilog
module _2_1_mux (
  input  I1,
  input  I2,
  input  I3,
  output O1
);

  wire and_1_out, and_2_out, not_1_out;

  not not_1 (not_1_out, I3);
  and and_1 (and_1_out, I1, not_1_out);
  and and_2 (and_2_out, I2, I3);
  or or_1 (O1, and_1_out, and_2_out);
endmodule

module _4_1_mux (
  input  in_1,
  input  in_2,
  input  in_3,
  input  in_4,
  input  in_5,
  input  in_6,
  output out_7
);

  wire n2_1_mux_1_o1, n2_1_mux_2_o1;

  // Probe on n2_1_mux_1_o1
  _2_1_mux u_2_1_mux_1 (.I1(in_1), .I2(in_2), .I3(in_5), .O1(n2_1_mux_1_o1));
  _2_1_mux u_2_1_mux_2 (.I1(in_3), .I2(in_4), .I3(in_5), .O1(n2_1_mux_2_o1));
  // Probe on n2_1_mux_2_o1
  _2_1_mux u_2_1_mux_3 (.I1(n2_1_mux_1_o1), .I2(n2_1_mux_2_o1), .I3(in_6), .O1(out_7));
endmodule
