// Logisim project test2.circ as structural Verilog: 1 circuit, main circuit responder
module responder (
  input  _1,
  input  _2,
  input  _3,
  input  referee,
  output [2:0] out_5
);

  wire _1_t, _2_t, _3_t, clock_1_out;
  wire [2:0] register_1_q, register_2_q, register_3_q;

  Clock clock_1 (.out(clock_1_out));
  Register #(.width(3)) register_1 (.D(3'b100), .en(_3_t), .Q(register_1_q), .clk(_1));  // open: clr
  Register #(.width(3)) register_2 (.D(3'b010), .en(_3_t), .Q(register_2_q), .clk(_2));  // open: clr
  Register #(.width(3)) register_3 (.D(3'b001), .en(_3_t), .Q(register_3_q), .clk(_3));  // open: clr
  Register #(.width(1)) register_4 (.D(referee), .Q(_2_t), .clk(clock_1_out));  // open: en, clr
  assign out_5 = register_1_q | register_2_q | register_3_q;  // OR_Gate or_1, 3 bits wide
  and and_1 (_3_t, _1_t, _2_t);
  Comparator #(.width(3)) comparator_1 (.a(out_5), .b(3'b000), .eq(_1_t));  // open: gt, lt
endmodule
