// Logisim project 周文钰CPU.circ as structural Verilog
module \指令解码  (
  input  [31:0] in_1,
  output RegWrite,
  output RegDst,
  output ALUSrc,
  output MemWrite,
  output branch,
  output jump,
  output MemtoReg,
  output \signed ,
  output [1:0] ALUop
);

  wire addu, bit_extender_1_out, not_1_out, not_2_out, not_3_out, not_4_out, not_5_out, not_6_out, not_7_out,
       not_8_out, or_6_out, ori, r, subu;
  wire [1:0] multiplexer_1_out, PCop;
  wire [31:0] compare;

  not not_1 (not_1_out, in_1[28]);
  and and_1 (r, not_1_out, not_2_out);
  not not_2 (not_2_out, in_1[27]);
  and and_2 (ori, in_1[29], not_3_out);
  not not_3 (not_3_out, in_1[27]);
  and and_3 (MemtoReg, in_1[31], not_4_out);
  not not_4 (not_4_out, in_1[29]);
  and and_4 (MemWrite, in_1[29], not_5_out);
  not not_5 (not_5_out, in_1[28]);
  and and_5 (jump, in_1[27], not_6_out);
  not not_6 (not_6_out, in_1[26]);
  not not_7 (not_7_out, in_1[29]);
  and and_6 (branch, not_7_out, in_1[28]);
  or or_1 (RegDst, addu, subu);
  or or_2 (\signed , MemtoReg, MemWrite);
  or or_3 (ALUSrc, MemtoReg, MemWrite, ori);
  not not_8 (not_8_out, in_1[1]);
  or or_4 (ALUop[1], ori, branch);
  and and_7 (addu, r, not_8_out);
  and and_8 (subu, in_1[1], r);
  or or_5 (ALUop[0], subu, branch);
  Multiplexer #(.width(2)) multiplexer_1 (.in0(2'b10), .in1(2'b01), .out(multiplexer_1_out), .sel(branch));  // open: en
  Bit_Extender #(.in_width(32), .out_width(1)) bit_extender_1 (.in(compare), .out(bit_extender_1_out));
  Multiplexer #(.width(2)) multiplexer_2 (
    .in0(2'b00), .in1(multiplexer_1_out), .out(PCop), .sel(or_6_out));  // open: en
  or or_6 (or_6_out, bit_extender_1_out, jump);
  or or_7 (RegWrite, MemtoReg, ori, addu, subu);

  // Other names for the same wires on the sheet: beq = branch; funct[5:0] = in_1[5:0]; opcode[5:0] = in_1[31:26];
  //   j = jump; lw = MemtoReg; sw = MemWrite
endmodule

module GRF (
  input  clk,
  input  reset,
  input  regWrite,
  input  [31:0] WD,
  input  [4:0] A1,
  input  [4:0] A3,
  input  [4:0] A2,
  output [31:0] RD1,
  output [31:0] RD2
);

  wire [31:0] _1, _2, _3, _4, _5, _6, _7, _8, _9, _10, _11, _12, _13, _14, _15, _16, _17, _18, _19, _20, _21,
       _22, _23, _24, _25, _26, _27, _28, _29, _30, _31, demultiplexer_1_out0, out0, out1, out2, out3, out4,
       out5, out6, out7, out8, out9, out10, out11, out12, out13, out14, out15, out16, out17, out18, out19,
       out20, out21, out22, out23, out24, out25, out26, out27, out28, out29, out30, out31;

  Register #(.width(32)) register_1 (.D({32{1'b0}}), .en(regWrite), .Q(out0), .clk(clk), .clr(reset));
  Register #(.width(32)) register_2 (.D(_1), .en(regWrite), .Q(out1), .clk(clk), .clr(reset));
  Multiplexer #(.select(5), .width(32)) multiplexer_1 (
    .in0(out0), .in1(out1), .in2(out2), .in3(out3), .in4(out4), .in5(out5), .in6(out6), .in7(out7),
    .in8(out8), .in9(out9), .in10(out10), .in11(out11), .in12(out12), .in13(out13), .in14(out14),
    .in15(out15), .in16(out16), .in17(out17), .in18(out18), .in19(out19), .in20(out20), .in21(out21),
    .in22(out22), .in23(out23), .in24(out24), .in25(out25), .in26(out26), .in27(out27), .in28(out28),
    .in29(out29), .in30(out30), .in31(out31), .out(RD1), .sel(A1));  // open: en
  Register #(.width(32)) register_3 (.D(_2), .en(regWrite), .Q(out2), .clk(clk), .clr(reset));
  Register #(.width(32)) register_4 (.D(_3), .en(regWrite), .Q(out3), .clk(clk), .clr(reset));
  Register #(.width(32)) register_5 (.D(_4), .en(regWrite), .Q(out4), .clk(clk), .clr(reset));
  Register #(.width(32)) register_6 (.D(_5), .en(regWrite), .Q(out5), .clk(clk), .clr(reset));
  Multiplexer #(.select(5), .width(32)) multiplexer_2 (
    .in0(out0), .in1(out1), .in2(out2), .in3(out3), .in4(out4), .in5(out5), .in6(out6), .in7(out7),
    .in8(out8), .in9(out9), .in10(out10), .in11(out11), .in12(out12), .in13(out13), .in14(out14),
    .in15(out15), .in16(out16), .in17(out17), .in18(out18), .in19(out19), .in20(out20), .in21(out21),
    .in22(out22), .in23(out23), .in24(out24), .in25(out25), .in26(out26), .in27(out27), .in28(out28),
    .in29(out29), .in30(out30), .in31(out31), .out(RD2), .sel(A2));  // open: en
  Register #(.width(32)) register_7 (.D(_6), .en(regWrite), .Q(out6), .clk(clk), .clr(reset));
  Register #(.width(32)) register_8 (.D(_7), .en(regWrite), .Q(out7), .clk(clk), .clr(reset));
  Register #(.width(32)) register_9 (.D(_8), .en(regWrite), .Q(out8), .clk(clk), .clr(reset));
  Register #(.width(32)) register_10 (.D(_9), .en(regWrite), .Q(out9), .clk(clk), .clr(reset));
  Demultiplexer #(.select(5), .width(32)) demultiplexer_1 (
    .out0(demultiplexer_1_out0), .out1(_1), .out2(_2), .out3(_3), .out4(_4), .out5(_5), .out6(_6), .out7(_7),
    .out8(_8), .out9(_9), .out10(_10), .out11(_11), .out12(_12), .out13(_13), .out14(_14), .out15(_15),
    .out16(_16), .out17(_17), .out18(_18), .out19(_19), .out20(_20), .out21(_21), .out22(_22), .out23(_23),
    .out24(_24), .out25(_25), .out26(_26), .out27(_27), .out28(_28), .out29(_29), .out30(_30), .out31(_31),
    .in(WD), .sel(A3));  // open: en
  Register #(.width(32)) register_11 (.D(_10), .en(regWrite), .Q(out10), .clk(clk), .clr(reset));
  Register #(.width(32)) register_12 (.D(_11), .en(regWrite), .Q(out11), .clk(clk), .clr(reset));
  Register #(.width(32)) register_13 (.D(_12), .en(regWrite), .Q(out12), .clk(clk), .clr(reset));
  Register #(.width(32)) register_14 (.D(_13), .en(regWrite), .Q(out13), .clk(clk), .clr(reset));
  Register #(.width(32)) register_15 (.D(_14), .en(regWrite), .Q(out14), .clk(clk), .clr(reset));
  Register #(.width(32)) register_16 (.D(_15), .en(regWrite), .Q(out15), .clk(clk), .clr(reset));
  Register #(.width(32)) register_17 (.D(_16), .en(regWrite), .Q(out16), .clk(clk), .clr(reset));
  Register #(.width(32)) register_18 (.D(_17), .en(regWrite), .Q(out17), .clk(clk), .clr(reset));
  Register #(.width(32)) register_19 (.D(_18), .en(regWrite), .Q(out18), .clk(clk), .clr(reset));
  Register #(.width(32)) register_20 (.D(_19), .en(regWrite), .Q(out19), .clk(clk), .clr(reset));
  Register #(.width(32)) register_21 (.D(_20), .en(regWrite), .Q(out20), .clk(clk), .clr(reset));
  Register #(.width(32)) register_22 (.D(_21), .en(regWrite), .Q(out21), .clk(clk), .clr(reset));
  Register #(.width(32)) register_23 (.D(_22), .en(regWrite), .Q(out22), .clk(clk), .clr(reset));
  Register #(.width(32)) register_24 (.D(_23), .en(regWrite), .Q(out23), .clk(clk), .clr(reset));
  Register #(.width(32)) register_25 (.D(_24), .en(regWrite), .Q(out24), .clk(clk), .clr(reset));
  Register #(.width(32)) register_26 (.D(_25), .en(regWrite), .Q(out25), .clk(clk), .clr(reset));
  Register #(.width(32)) register_27 (.D(_26), .en(regWrite), .Q(out26), .clk(clk), .clr(reset));
  Register #(.width(32)) register_28 (.D(_27), .en(regWrite), .Q(out27), .clk(clk), .clr(reset));
  Register #(.width(32)) register_29 (.D(_28), .en(regWrite), .Q(out28), .clk(clk), .clr(reset));
  Register #(.width(32)) register_30 (.D(_29), .en(regWrite), .Q(out29), .clk(clk), .clr(reset));
  Register #(.width(32)) register_31 (.D(_30), .en(regWrite), .Q(out30), .clk(clk), .clr(reset));
  Register #(.width(32)) register_32 (.D(_31), .en(regWrite), .Q(out31), .clk(clk), .clr(reset));
endmodule

module ALU (
  input  [31:0] A,
  input  [31:0] B,
  input  [1:0] ALUop,
  output [31:0] ALUresult,
  output [31:0] out_5
);

  wire comparator_1_eq;
  wire [31:0] addu, ori, sub;

  Adder #(.width(32)) adder_1 (.a(A), .b(B), .out(addu));  // open: cin, cout
  Subtractor #(.width(32)) subtractor_1 (.a(A), .b(B), .out(sub));  // open: bin, bout
  assign ori = A | B;  // OR_Gate or_1, 32 bits wide
  Comparator #(.width(32)) comparator_1 (.a(A), .b(B), .eq(comparator_1_eq));  // open: gt, lt
  assign out_5 = {{31{1'b0}}, comparator_1_eq};  // Bit_Extender bit_extender_1
  Multiplexer #(.select(2), .width(32)) multiplexer_1 (
    .in0(addu), .in1(sub), .in2(ori), .in3(out_5), .out(ALUresult), .sel(ALUop));  // open: en

  // Other names for the same wires on the sheet: compare[31:0] = out_5

  // Notes on the sheet:
  //   A=B，返回1
endmodule

module SPLT (
  input  [31:0] instruction
);


  // Other names for the same wires on the sheet: funct[5:0] = instruction[5:0]; imm[15:0] = instruction[15:0];
  //   shamt[4:0] = instruction[10:6]; Rd[4:0] = instruction[15:11]; Rt[4:0] = instruction[20:16];
  //   Rs[4:0] = instruction[25:21]; opcode[5:0] = instruction[31:26]
endmodule

module PC (
  input  clk,
  input  [31:0] DI,
  input  reset,
  output [31:0] DO
);

  Register #(.width(32)) register_1 (.D(DI), .Q(DO), .clk(clk), .clr(reset));  // open: en
endmodule

module EXT (
  input  \signed ,
  input  [15:0] imm16,
  output [31:0] EXT32
);

  wire [31:0] bit_extender_1_out, bit_extender_2_out;

  assign bit_extender_1_out = {{16{1'b0}}, imm16};  // Bit_Extender bit_extender_1
  assign bit_extender_2_out = {{16{imm16[15]}}, imm16};  // Bit_Extender bit_extender_2
  Multiplexer #(.width(32)) multiplexer_1 (
    .in0(bit_extender_1_out), .in1(bit_extender_2_out), .out(EXT32), .sel(\signed ));  // open: en
endmodule

module IM (
  input  [31:0] Address,
  output [31:0] Data
);

  ROM #(.addrWidth(5), .dataWidth(32)) rom_1 (.addr(Address[6:2]), .data(Data));  // open: sel
endmodule

module DM (
  input  clk,
  input  [31:0] in_2,
  input  [31:0] in_3,
  input  reset,
  input  regWrite,
  output [31:0] out_6
);

  RAM #(.addrWidth(5), .dataWidth(32), .bus("separate")) ram_1 (
    .addr(in_2[6:2]), .din(in_3), .data(out_6), .str(regWrite), .clk(clk), .clr(reset));  // open: sel, ld

  // Other names for the same wires on the sheet: Address[31:0] = in_2; RD[31:0] = out_6; WD[31:0] = in_3
endmodule

module NPC (
  input  [1:0] in_1,
  input  [31:0] in_2,
  input  [25:0] in_3,
  output [31:0] out_4,
  output [31:0] out_5
);

  wire [31:0] bit_extender_1_out, shifter_1_out;

  assign bit_extender_1_out = {{16{in_3[15]}}, in_3[15:0]};  // Bit_Extender bit_extender_1
  Adder #(.width(32)) adder_1 (.a(in_2), .b(32'h4), .out(out_5));  // open: cin, cout
  Shifter #(.width(32)) shifter_1 (.in(bit_extender_1_out), .\dist (5'b00010), .out(shifter_1_out));
  Adder #(.width(32)) adder_2 (.a(out_5), .b(shifter_1_out), .out(out_4));  // open: cin, cout
  Multiplexer #(.select(2), .width(32)) multiplexer_1 (
    .in0(out_5), .in1(out_4), .in2({in_2[31:28], in_3, 2'b00}), .sel(in_1));  // open: in3, out, en

  // Other names for the same wires on the sheet: imm26[25:0] = in_3; PC[31:0] = in_2; NPC[31:0] = out_4;
  //   PC4[31:0] = out_5; PCop[1:0] = in_1
endmodule
